// Logisim project GPU Compute Module_WW.circ as structural Verilog: 3 circuits, main circuit gpu_compute_module
// GPU\nCOMPUTE MODULE
module gpu_compute_module (
  input  [15:0] str0,
  input  [15:0] str1,
  input  [15:0] str2,
  input  [15:0] str3,
  input  [15:0] str4,
  input  [15:0] str5,
  input  [15:0] str6,
  input  [15:0] str7,
  input  [15:0] str8,
  input  [15:0] str9,
  input  [15:0] str10,
  input  [15:0] str11,
  input  [15:0] str12,
  input  [15:0] str13,
  input  [15:0] str14,
  input  [15:0] str15,
  input  [15:0] str16,
  input  [15:0] str17,
  input  [15:0] str18,
  input  [15:0] str19,
  input  [15:0] str20,
  input  [15:0] str21,
  input  [15:0] str22,
  input  [15:0] str23,
  input  [15:0] str24,
  input  [15:0] str25,
  input  [15:0] str26,
  input  [15:0] str27,
  input  [15:0] str28,
  input  [15:0] str29,
  input  [15:0] str30,
  input  [15:0] str31,
  input  [17:0] str_right,
  input  [17:0] str_left,
  input  [31:0] str_up,
  input  [31:0] str_down,
  output [15:0] next_gen0,
  output [15:0] next_gen1,
  output [15:0] next_gen2,
  output [15:0] next_gen3,
  output [15:0] next_gen4,
  output [15:0] next_gen5,
  output [15:0] next_gen6,
  output [15:0] next_gen7,
  output [15:0] next_gen8,
  output [15:0] next_gen9,
  output [15:0] next_gen10,
  output [15:0] next_gen11,
  output [15:0] next_gen12,
  output [15:0] next_gen13,
  output [15:0] next_gen14,
  output [15:0] next_gen15,
  output [15:0] next_gen15_2,
  output [15:0] next_gen17,
  output [15:0] next_gen18,
  output [15:0] next_gen19,
  output [15:0] next_gen20,
  output [15:0] next_gen21,
  output [15:0] next_gen22,
  output [15:0] next_gen23,
  output [15:0] next_gen24,
  output [15:0] next_gen25,
  output [15:0] next_gen26,
  output [15:0] next_gen27,
  output [15:0] next_gen28,
  output [15:0] next_gen29,
  output [15:0] next_gen30,
  output [15:0] next_gen31
);

  cu_block _0 (
    .left_row(str_left[16:1]), .center_row(str0), .right_row(str1),
    .cycle({str_left[17], str_up[1:0], str_left[0], str_down[1:0]}), .computed_row(next_gen0));
  cu_block _1 (
    .left_row(str0), .center_row(str1), .right_row(str2), .cycle({str_up[2:0], str_down[2:0]}),
    .computed_row(next_gen1));
  cu_block _2 (
    .left_row(str1), .center_row(str2), .right_row(str3), .cycle({str_up[3:1], str_down[3:1]}),
    .computed_row(next_gen2));
  cu_block _3 (
    .left_row(str2), .center_row(str3), .right_row(str4), .cycle({str_up[4:2], str_down[4:2]}),
    .computed_row(next_gen3));
  cu_block _4 (
    .left_row(str3), .center_row(str4), .right_row(str5), .cycle({str_up[5:3], str_down[5:3]}),
    .computed_row(next_gen4));
  cu_block _5 (
    .left_row(str4), .center_row(str5), .right_row(str6), .cycle({str_up[6:4], str_down[6:4]}),
    .computed_row(next_gen5));
  cu_block _6 (
    .left_row(str5), .center_row(str6), .right_row(str7), .cycle({str_up[7:5], str_down[7:5]}),
    .computed_row(next_gen6));
  cu_block _7 (
    .left_row(str6), .center_row(str7), .right_row(str8), .cycle({str_up[8:6], str_down[8:6]}),
    .computed_row(next_gen7));
  cu_block _8 (
    .left_row(str7), .center_row(str8), .right_row(str9), .cycle({str_up[9:7], str_down[9:7]}),
    .computed_row(next_gen8));
  cu_block _9 (
    .left_row(str8), .center_row(str9), .right_row(str10), .cycle({str_up[10:8], str_down[10:8]}),
    .computed_row(next_gen9));
  cu_block _10 (
    .left_row(str9), .center_row(str10), .right_row(str11), .cycle({str_up[11:9], str_down[11:9]}),
    .computed_row(next_gen10));
  cu_block _11 (
    .left_row(str10), .center_row(str11), .right_row(str12), .cycle({str_up[12:10], str_down[12:10]}),
    .computed_row(next_gen11));
  cu_block _12 (
    .left_row(str11), .center_row(str12), .right_row(str13), .cycle({str_up[13:11], str_down[13:11]}),
    .computed_row(next_gen12));
  cu_block _13 (
    .left_row(str12), .center_row(str13), .right_row(str14), .cycle({str_up[14:12], str_down[14:12]}),
    .computed_row(next_gen13));
  cu_block _14 (
    .left_row(str13), .center_row(str14), .right_row(str15), .cycle({str_up[15:13], str_down[15:13]}),
    .computed_row(next_gen14));
  cu_block _16 (
    .left_row(str15), .center_row(str16), .right_row(str17), .cycle({str_up[17:15], str_down[17:15]}),
    .computed_row(next_gen15_2));
  cu_block _15 (
    .left_row(str14), .center_row(str15), .right_row(str16), .cycle({str_up[16:14], str_down[16:14]}),
    .computed_row(next_gen15));
  cu_block _17 (
    .left_row(str16), .center_row(str17), .right_row(str18), .cycle({str_up[18:16], str_down[18:16]}),
    .computed_row(next_gen17));
  cu_block _18 (
    .left_row(str17), .center_row(str18), .right_row(str19), .cycle({str_up[19:17], str_down[19:17]}),
    .computed_row(next_gen18));
  cu_block _19 (
    .left_row(str18), .center_row(str19), .right_row(str20), .cycle({str_up[20:18], str_down[20:18]}),
    .computed_row(next_gen19));
  cu_block _20 (
    .left_row(str19), .center_row(str20), .right_row(str21), .cycle({str_up[21:19], str_down[21:19]}),
    .computed_row(next_gen20));
  cu_block _21 (
    .left_row(str20), .center_row(str21), .right_row(str22), .cycle({str_up[22:20], str_down[22:20]}),
    .computed_row(next_gen21));
  cu_block _22 (
    .left_row(str21), .center_row(str22), .right_row(str23), .cycle({str_up[23:21], str_down[23:21]}),
    .computed_row(next_gen22));
  cu_block _24 (
    .left_row(str23), .center_row(str24), .right_row(str25), .cycle({str_up[25:23], str_down[25:23]}),
    .computed_row(next_gen24));
  cu_block _23 (
    .left_row(str22), .center_row(str23), .right_row(str24), .cycle({str_up[24:22], str_down[24:22]}),
    .computed_row(next_gen23));
  cu_block _25 (
    .left_row(str24), .center_row(str25), .right_row(str26), .cycle({str_up[26:24], str_down[26:24]}),
    .computed_row(next_gen25));
  cu_block _26 (
    .left_row(str25), .center_row(str26), .right_row(str27), .cycle({str_up[27:25], str_down[27:25]}),
    .computed_row(next_gen26));
  cu_block _27 (
    .left_row(str26), .center_row(str27), .right_row(str28), .cycle({str_up[28:26], str_down[28:26]}),
    .computed_row(next_gen27));
  cu_block _28 (
    .left_row(str27), .center_row(str28), .right_row(str29), .cycle({str_up[29:27], str_down[29:27]}),
    .computed_row(next_gen28));
  cu_block _29 (
    .left_row(str28), .center_row(str29), .right_row(str30), .cycle({str_up[30:28], str_down[30:28]}),
    .computed_row(next_gen29));
  cu_block _30 (
    .left_row(str29), .center_row(str30), .right_row(str31), .cycle({str_up[31:29], str_down[31:29]}),
    .computed_row(next_gen30));
  cu_block _31 (
    .left_row(str30), .center_row(str31), .right_row(str_right[16:1]),
    .cycle({str_right[17], str_up[31:30], str_right[0], str_down[31:30]}), .computed_row(next_gen31));

  // Other names for the same wires on the sheet: strd[31:0] = str_down; stru[31:0] = str_up;
  //   strr0_17[1:0] = {str_right[17], str_right[0]}; strl_1_16[15:0] = str_left[16:1];
  //   strr1_16[15:0] = str_right[16:1]
endmodule

// COMPUTE\nUNITS
module cu_block (
  input  [15:0] left_row,
  input  [15:0] center_row,
  input  [15:0] right_row,
  input  [5:0] cycle,
  output [15:0] computed_row
);

  cu _15 (
    .\cell (center_row[15]),
    .neighbors({cycle[4:3], right_row[15:14], center_row[14], left_row[14], left_row[15], cycle[5]}),
    .new_gen(computed_row[15]));
  cu _14 (
    .\cell (center_row[14]),
    .neighbors({center_row[15], right_row[15:13], center_row[13], left_row[13], left_row[14], left_row[15]}),
    .new_gen(computed_row[14]));
  cu _13 (
    .\cell (center_row[13]),
    .neighbors({center_row[14], right_row[14:12], center_row[12], left_row[12], left_row[13], left_row[14]}),
    .new_gen(computed_row[13]));
  cu _12 (
    .\cell (center_row[12]),
    .neighbors({center_row[13], right_row[13:11], center_row[11], left_row[11], left_row[12], left_row[13]}),
    .new_gen(computed_row[12]));
  cu _11 (
    .\cell (center_row[11]),
    .neighbors({center_row[12], right_row[12:10], center_row[10], left_row[10], left_row[11], left_row[12]}),
    .new_gen(computed_row[11]));
  cu _10 (
    .\cell (center_row[10]),
    .neighbors({center_row[11], right_row[11:9], center_row[9], left_row[9], left_row[10], left_row[11]}),
    .new_gen(computed_row[10]));
  cu _9 (
    .\cell (center_row[9]),
    .neighbors({center_row[10], right_row[10:8], center_row[8], left_row[8], left_row[9], left_row[10]}),
    .new_gen(computed_row[9]));
  cu _8 (
    .\cell (center_row[8]),
    .neighbors({center_row[9], right_row[9:7], center_row[7], left_row[7], left_row[8], left_row[9]}),
    .new_gen(computed_row[8]));
  cu _7 (
    .\cell (center_row[7]),
    .neighbors({center_row[8], right_row[8:6], center_row[6], left_row[6], left_row[7], left_row[8]}),
    .new_gen(computed_row[7]));
  cu _6 (
    .\cell (center_row[6]),
    .neighbors({center_row[7], right_row[7:5], center_row[5], left_row[5], left_row[6], left_row[7]}),
    .new_gen(computed_row[6]));
  cu _5 (
    .\cell (center_row[5]),
    .neighbors({center_row[6], right_row[6:4], center_row[4], left_row[4], left_row[5], left_row[6]}),
    .new_gen(computed_row[5]));
  cu _4 (
    .\cell (center_row[4]),
    .neighbors({center_row[5], right_row[5:3], center_row[3], left_row[3], left_row[4], left_row[5]}),
    .new_gen(computed_row[4]));
  cu _3 (
    .\cell (center_row[3]),
    .neighbors({center_row[4], right_row[4:2], center_row[2], left_row[2], left_row[3], left_row[4]}),
    .new_gen(computed_row[3]));
  cu _2 (
    .\cell (center_row[2]),
    .neighbors({center_row[3], right_row[3:1], center_row[1], left_row[1], left_row[2], left_row[3]}),
    .new_gen(computed_row[2]));
  cu _1 (
    .\cell (center_row[1]),
    .neighbors({center_row[2], right_row[2:0], center_row[0], left_row[0], left_row[1], left_row[2]}),
    .new_gen(computed_row[1]));
  cu _0 (
    .\cell (center_row[0]),
    .neighbors({center_row[1], right_row[1:0], cycle[0], cycle[1], cycle[2], left_row[0], left_row[1]}),
    .new_gen(computed_row[0]));

  // Other names for the same wires on the sheet: lr_15 = left_row[15]; lr_14 = left_row[14]; lr_13 = left_row[13];
  //   lr_12 = left_row[12]; lr_11 = left_row[11]; lr_10 = left_row[10]; lr_9 = left_row[9]; lr_8 = left_row[8];
  //   cr_8 = center_row[8]; lr_7 = left_row[7]; cr_7 = center_row[7]; lr_6 = left_row[6]; cr_6 = center_row[6];
  //   lr_5 = left_row[5]; cr_5 = center_row[5]; lr_4 = left_row[4]; rr_4 = right_row[4]; cr_4 = center_row[4];
  //   lr_3 = left_row[3]; rr_3 = right_row[3]; cr_3 = center_row[3]; lr_2 = left_row[2]; cr_0 = center_row[0];
  //   rr_2 = right_row[2]; cr_2 = center_row[2]; lr_1 = left_row[1]; lr_0 = left_row[0]; rr_0 = right_row[0];
  //   rr_1 = right_row[1]; cr_1 = center_row[1]; cr_9 = center_row[9]; cr_10 = center_row[10]; cr_11 = center_row[11];
  //   cr_12 = center_row[12]; cr_13 = center_row[13]; cr_14 = center_row[14]; cr_15 = center_row[15];
  //   cu_0 = computed_row[0]; cu_1 = computed_row[1]; cu_2 = computed_row[2]; cu_3 = computed_row[3];
  //   cu_4 = computed_row[4]; cu_5 = computed_row[5]; cu_6 = computed_row[6]; cu_7 = computed_row[7];
  //   cu_8 = computed_row[8]; cu_9 = computed_row[9]; cu_10 = computed_row[10]; cu_11 = computed_row[11];
  //   cu_12 = computed_row[12]; cu_13 = computed_row[13]; cu_14 = computed_row[14]; cu_15 = computed_row[15];
  //   c_0 = cycle[0]; c_1 = cycle[1]; c_2 = cycle[2]; c_3 = cycle[3]; c_4 = cycle[4]; c_5 = cycle[5];
  //   rr_5 = right_row[5]; rr_6 = right_row[6]; rr_7 = right_row[7]; rr_8 = right_row[8]; rr_9 = right_row[9];
  //   rr_10 = right_row[10]; rr_11 = right_row[11]; rr_12 = right_row[12]; rr_13 = right_row[13];
  //   rr_14 = right_row[14]; rr_15 = right_row[15]
endmodule

// CU
module cu (
  input  \cell ,
  input  [7:0] neighbors,
  output new_gen
);

  wire comparator_1_eq, comparator_2_eq, or_1_out;
  wire [3:0] bitadder_1_out;

  BitAdder bitadder_1 (.in0(neighbors), .out(bitadder_1_out));
  Comparator #(.width(4), .mode("unsigned")) comparator_1 (
    .a(bitadder_1_out), .b(4'b0011), .eq(comparator_1_eq));  // open: gt, lt
  Comparator #(.width(4), .mode("unsigned")) comparator_2 (
    .a(bitadder_1_out), .b(4'b0010), .eq(comparator_2_eq));  // open: gt, lt
  or or_1 (or_1_out, comparator_1_eq, comparator_2_eq);
  Multiplexer multiplexer_1 (.in0(comparator_1_eq), .in1(or_1_out), .out(new_gen), .sel(\cell ));  // open: en
endmodule
