// Logisim project counter.circ as structural Verilog: 4 circuits, main circuit main
module main (
  input  clock,
  input  active,
  input  reset
);

  wire _0, _1, _2, _3, _4, _5, _6, _7, _8, _9, _10, _11, _12, _13, _14, _15, t_ff_1_qn, t_ff_2_qn, t_ff_3_qn,
       t_ff_4_qn, t_ff_5_qn, t_ff_6_qn, t_ff_7_qn, t_ff_8_qn, t_ff_9_qn, t_ff_10_qn, t_ff_11_qn, t_ff_12_qn,
       t_ff_13_qn, t_ff_14_qn, t_ff_15_qn;
  wire [15:0] del_1_hundred, del_1_one, del_1_ten, del_1_ten_thousand, del_1_thousand;

  T_Flip_Flop t_ff_1 (.clk(clock), .T(active), .Q(_0), .Qn(t_ff_1_qn), .reset(reset));  // open: preset, en
  hton hton_1 (.in_1(del_1_thousand));  // open: a, b, c, d, e, f, g
  hton hton_2 (.in_1(del_1_ten_thousand));  // open: a, b, c, d, e, f, g
  del del_1 (
    .one(del_1_one), .ten(del_1_ten), .hundred(del_1_hundred), .thousand(del_1_thousand),
    .ten_thousand(del_1_ten_thousand),
    .in_1({_15, _14, _13, _12, _11, _10, _9, _8, _7, _6, _5, _4, _3, _2, _1, _0}));
  T_Flip_Flop t_ff_2 (.clk(t_ff_1_qn), .T(active), .Q(_1), .Qn(t_ff_2_qn), .reset(reset));  // open: preset, en
  hton hton_3 (.in_1(del_1_hundred));  // open: a, b, c, d, e, f, g
  hton hton_4 (.in_1(del_1_ten));  // open: a, b, c, d, e, f, g
  T_Flip_Flop t_ff_3 (.clk(t_ff_2_qn), .T(active), .Q(_2), .Qn(t_ff_3_qn), .reset(reset));  // open: preset, en
  hton hton_5 (.in_1(del_1_one));  // open: a, b, c, d, e, f, g
  T_Flip_Flop t_ff_4 (.clk(t_ff_3_qn), .T(active), .Q(_3), .Qn(t_ff_4_qn), .reset(reset));  // open: preset, en
  T_Flip_Flop t_ff_5 (.clk(t_ff_4_qn), .T(active), .Q(_4), .Qn(t_ff_5_qn), .reset(reset));  // open: preset, en
  T_Flip_Flop t_ff_6 (.clk(t_ff_5_qn), .T(active), .Q(_5), .Qn(t_ff_6_qn), .reset(reset));  // open: preset, en
  T_Flip_Flop t_ff_7 (.clk(t_ff_6_qn), .T(active), .Q(_6), .Qn(t_ff_7_qn), .reset(reset));  // open: preset, en
  T_Flip_Flop t_ff_8 (.clk(t_ff_7_qn), .T(active), .Q(_7), .Qn(t_ff_8_qn), .reset(reset));  // open: preset, en
  T_Flip_Flop t_ff_9 (.clk(t_ff_8_qn), .T(active), .Q(_8), .Qn(t_ff_9_qn), .reset(reset));  // open: preset, en
  T_Flip_Flop t_ff_10 (.clk(t_ff_9_qn), .T(active), .Q(_9), .Qn(t_ff_10_qn), .reset(reset));  // open: preset, en
  T_Flip_Flop t_ff_11 (.clk(t_ff_10_qn), .T(active), .Q(_10), .Qn(t_ff_11_qn), .reset(reset));  // open: preset, en
  T_Flip_Flop t_ff_12 (.clk(t_ff_11_qn), .T(active), .Q(_11), .Qn(t_ff_12_qn), .reset(reset));  // open: preset, en
  T_Flip_Flop t_ff_13 (.clk(t_ff_12_qn), .T(active), .Q(_12), .Qn(t_ff_13_qn), .reset(reset));  // open: preset, en
  T_Flip_Flop t_ff_14 (.clk(t_ff_13_qn), .T(active), .Q(_13), .Qn(t_ff_14_qn), .reset(reset));  // open: preset, en
  T_Flip_Flop t_ff_15 (.clk(t_ff_14_qn), .T(active), .Q(_14), .Qn(t_ff_15_qn), .reset(reset));  // open: preset, en
  T_Flip_Flop t_ff_16 (.clk(t_ff_15_qn), .T(active), .Q(_15), .reset(reset));  // open: Qn, preset, en
endmodule

module hton (
  input  [15:0] in_1,
  output a,
  output b,
  output c,
  output d,
  output e,
  output f,
  output g
);

  wire and_1_out, and_2_out, and_3_out, and_4_out, and_5_out, and_6_out, and_7_out, and_8_out, and_9_out,
       and_10_out, and_11_out, and_12_out, and_13_out, and_14_out, and_15_out, and_16_out, and_17_out,
       and_18_out, and_19_out, and_20_out, and_21_out, and_22_out, and_23_out, and_24_out, and_25_out,
       and_26_out, not_1_out, not_2_out, not_3_out, not_4_out, not_5_out, not_6_out, not_7_out, not_8_out,
       not_9_out, not_10_out, not_11_out, not_12_out, not_13_out, not_14_out, not_15_out, not_16_out,
       not_17_out, not_18_out, not_19_out, not_20_out, not_21_out, not_22_out, not_23_out, not_24_out,
       not_25_out, not_26_out, not_27_out, not_28_out, not_29_out, not_30_out, not_31_out, not_32_out,
       not_33_out, not_34_out, not_35_out, not_36_out, not_37_out, not_38_out, not_39_out, not_40_out,
       not_41_out, not_42_out, not_43_out, not_44_out, not_45_out, not_46_out, not_47_out, not_48_out,
       not_49_out, not_50_out, not_51_out, not_52_out, not_53_out, not_54_out, not_55_out, not_56_out,
       not_57_out, not_58_out, not_59_out, not_60_out, not_61_out, not_62_out, not_63_out, not_64_out,
       not_65_out, not_66_out, not_67_out, not_68_out, not_69_out, not_70_out, not_71_out, not_72_out,
       not_73_out, not_74_out, not_75_out, not_76_out, not_77_out, not_78_out, not_79_out, not_80_out,
       not_81_out, not_82_out, not_83_out, not_84_out, not_85_out, not_86_out;

  not not_1 (not_1_out, in_1[3]);
  not not_2 (not_2_out, in_1[2]);
  not not_3 (not_3_out, in_1[0]);
  not not_4 (not_4_out, in_1[3]);
  not not_5 (not_5_out, in_1[3]);
  not not_6 (not_6_out, in_1[2]);
  not not_7 (not_7_out, in_1[1]);
  not not_8 (not_8_out, in_1[1]);
  not not_9 (not_9_out, in_1[0]);
  not not_10 (not_10_out, in_1[0]);
  not not_11 (not_11_out, in_1[2]);
  not not_12 (not_12_out, in_1[1]);
  not not_13 (not_13_out, in_1[1]);
  not not_14 (not_14_out, in_1[2]);
  not not_15 (not_15_out, in_1[0]);
  not not_16 (not_16_out, in_1[3]);
  not not_17 (not_17_out, in_1[1]);
  not not_18 (not_18_out, in_1[2]);
  not not_19 (not_19_out, in_1[2]);
  not not_20 (not_20_out, in_1[3]);
  not not_21 (not_21_out, in_1[1]);
  not not_22 (not_22_out, in_1[2]);
  not not_23 (not_23_out, in_1[2]);
  not not_24 (not_24_out, in_1[3]);
  and and_1 (and_1_out, not_1_out, not_2_out, not_3_out);
  and and_2 (and_2_out, not_4_out, in_1[1]);
  and and_3 (and_3_out, not_5_out, in_1[2], in_1[0]);
  and and_4 (and_4_out, in_1[3], not_6_out, not_7_out);
  not not_25 (not_25_out, in_1[3]);
  and and_5 (and_5_out, not_25_out, not_26_out);
  not not_26 (not_26_out, in_1[2]);
  not not_27 (not_27_out, in_1[3]);
  not not_28 (not_28_out, in_1[1]);
  and and_6 (and_6_out, not_27_out, not_28_out, not_29_out);
  not not_29 (not_29_out, in_1[0]);
  not not_30 (not_30_out, in_1[2]);
  and and_7 (and_7_out, not_30_out, not_31_out);
  not not_31 (not_31_out, in_1[1]);
  not not_32 (not_32_out, in_1[3]);
  and and_8 (and_8_out, not_32_out, not_33_out, not_34_out);
  not not_33 (not_33_out, not_8_out);
  not not_34 (not_34_out, not_9_out);
  not not_35 (not_35_out, in_1[2]);
  and and_9 (and_9_out, not_35_out, not_36_out);
  not not_36 (not_36_out, in_1[1]);
  not not_37 (not_37_out, in_1[3]);
  and and_10 (and_10_out, not_37_out, not_38_out);
  not not_38 (not_38_out, not_10_out);
  not not_39 (not_39_out, in_1[3]);
  and and_11 (and_11_out, not_39_out, not_40_out);
  not not_40 (not_40_out, not_11_out);
  not not_41 (not_41_out, in_1[3]);
  not not_42 (not_42_out, in_1[2]);
  not not_43 (not_43_out, in_1[0]);
  not not_44 (not_44_out, in_1[3]);
  not not_45 (not_45_out, in_1[2]);
  not not_46 (not_46_out, not_12_out);
  not not_47 (not_47_out, in_1[3]);
  not not_48 (not_48_out, not_13_out);
  not not_49 (not_49_out, in_1[0]);
  not not_50 (not_50_out, in_1[3]);
  not not_51 (not_51_out, not_14_out);
  not not_52 (not_52_out, in_1[1]);
  not not_53 (not_53_out, not_15_out);
  not not_54 (not_54_out, not_16_out);
  not not_55 (not_55_out, in_1[2]);
  not not_56 (not_56_out, in_1[1]);
  not not_57 (not_57_out, in_1[2]);
  and and_12 (and_12_out, not_57_out, not_58_out, not_59_out);
  not not_58 (not_58_out, in_1[1]);
  not not_59 (not_59_out, in_1[0]);
  not not_60 (not_60_out, in_1[3]);
  not not_61 (not_61_out, not_17_out);
  and and_13 (and_13_out, not_60_out, not_61_out, not_62_out);
  not not_62 (not_62_out, in_1[0]);
  not not_63 (not_63_out, in_1[3]);
  and and_14 (and_14_out, not_63_out, not_64_out, not_65_out);
  not not_64 (not_64_out, in_1[1]);
  not not_65 (not_65_out, in_1[0]);
  not not_66 (not_66_out, in_1[3]);
  and and_15 (and_15_out, not_66_out, not_67_out, not_68_out);
  not not_67 (not_67_out, not_18_out);
  not not_68 (not_68_out, in_1[1]);
  not not_69 (not_69_out, in_1[3]);
  not not_70 (not_70_out, not_19_out);
  and and_16 (and_16_out, not_69_out, not_70_out, not_71_out);
  not not_71 (not_71_out, in_1[0]);
  not not_72 (not_72_out, not_20_out);
  and and_17 (and_17_out, not_72_out, not_73_out, not_74_out);
  not not_73 (not_73_out, in_1[2]);
  not not_74 (not_74_out, in_1[1]);
  not not_75 (not_75_out, in_1[3]);
  and and_18 (and_18_out, not_75_out, not_76_out, not_77_out);
  not not_76 (not_76_out, in_1[2]);
  not not_77 (not_77_out, not_21_out);
  not not_78 (not_78_out, in_1[3]);
  and and_19 (and_19_out, not_78_out, not_79_out, not_80_out);
  not not_79 (not_79_out, not_22_out);
  not not_80 (not_80_out, in_1[1]);
  not not_81 (not_81_out, in_1[3]);
  and and_20 (and_20_out, not_81_out, not_82_out, not_83_out);
  not not_82 (not_82_out, not_23_out);
  not not_83 (not_83_out, in_1[0]);
  not not_84 (not_84_out, not_24_out);
  not not_85 (not_85_out, in_1[2]);
  and and_21 (and_21_out, not_84_out, not_85_out, not_86_out);
  not not_86 (not_86_out, in_1[1]);
  or or_1 (a, and_1_out, and_2_out, and_3_out, and_4_out);
  or or_2 (b, and_5_out, and_6_out, and_7_out, and_8_out);
  or or_3 (c, and_9_out, and_10_out, and_11_out);
  and and_22 (and_22_out, not_41_out, not_42_out, not_43_out);
  and and_23 (and_23_out, not_44_out, not_45_out, not_46_out);
  and and_24 (and_24_out, not_47_out, not_48_out, not_49_out);
  and and_25 (and_25_out, not_50_out, not_51_out, not_52_out, not_53_out);
  and and_26 (and_26_out, not_54_out, not_55_out, not_56_out);
  or or_4 (e, and_12_out, and_13_out);
  or or_5 (f, and_14_out, and_15_out, and_16_out, and_17_out);
  or or_6 (g, and_18_out, and_19_out, and_20_out, and_21_out);
  or or_7 (d, and_22_out, and_23_out, and_24_out, and_25_out, and_26_out);
endmodule

module del (
  input  [15:0] in_1,
  output [15:0] one,
  output [15:0] ten,
  output [15:0] hundred,
  output [15:0] thousand,
  output [15:0] ten_thousand
);

  wire [15:0] divider_1_out, divider_2_out, divider_3_out, divider_4_out;

  // Probe on in_1
  Divider #(.width(16)) divider_1 (.a(in_1), .b(16'ha), .out(divider_1_out), .rem(one));  // open: upper
  // Probe on one
  Divider #(.width(16)) divider_2 (.a(divider_1_out), .b(16'ha), .out(divider_2_out), .rem(ten));  // open: upper
  // Probe on ten
  // Probe on hundred
  Divider #(.width(16)) divider_3 (.a(divider_2_out), .b(16'ha), .out(divider_3_out), .rem(hundred));  // open: upper
  Divider #(.width(16)) divider_4 (.a(divider_3_out), .b(16'ha), .out(divider_4_out), .rem(thousand));  // open: upper
  // Probe on thousand
  Divider #(.width(16)) divider_5 (.a(divider_4_out), .b(16'ha), .rem(ten_thousand));  // open: out, upper
  // Probe on ten_thousand
endmodule

module counter (
);

  main main_1 ();  // open: clock, active, reset
endmodule
