// Logisim project main.circ as structural Verilog: 4 circuits, main circuit main
module main (
  input  Hold
);

  wire _0, _1, _2, _3, _4, _5, _6, _7, _8, _9, _10, _11, _12, _13, _14, _15, bashni, \bit ,
       but_control_1_irq, cdm16_1_p3, cdm16_1_p5, cdm16_1_p9, cdm16_1_p12, cdm16_1_p13, cdm16_1_p14,
       cdm16_1_p15, cdm16_1_p16, cl, comparator_1_eq, down, hton_1_a, hton_1_b, hton_1_c, hton_1_d, hton_1_e,
       hton_1_f, hton_1_g, hton_2_a, hton_2_b, hton_2_c, hton_2_d, hton_2_e, hton_2_f, hton_2_g, hton_3_a,
       hton_3_b, hton_3_c, hton_3_d, hton_3_e, hton_3_f, hton_3_g, hton_4_a, hton_4_b, hton_4_c, hton_4_d,
       hton_4_e, hton_4_f, hton_4_g, hton_5_a, hton_5_b, hton_5_c, hton_5_d, hton_5_e, hton_5_f, hton_5_g,
       ld, left, life_on_mark, mem, not_1_out, not_2_out, or_1_out, plane, read, right, set_col, set_op,
       t_ff_1_qn, t_ff_2_qn, t_ff_3_qn, t_ff_4_qn, t_ff_5_qn, t_ff_6_qn, t_ff_7_qn, t_ff_8_qn, t_ff_9_qn,
       t_ff_10_qn, t_ff_11_qn, t_ff_12_qn, t_ff_13_qn, t_ff_14_qn, t_ff_15_qn, up;
  wire [2:1] CR3IN, CR3OUT, CR4IN, CR4OUT, CR5IN, CR5OUT, CR6IN, CR6OUT;
  wire [3:0] CR1IN, CR1OUT, CR2IN, CR2OUT;
  wire [4:0] screen_control_1_cslr_2, screen_control_2_cslr_2, screen_control_3_cslr_2,
       screen_control_4_cslr_2;
  wire [4:1] cslrn;
  wire [5:0] vec;
  wire [15:0] addr, cdm16_1_p21, cdm16_1_p22, data, del_1_hundred, del_1_one, del_1_ten, del_1_ten_thousand,
       del_1_thousand, L1left, L1right, L2left, L2right, L3left, L3right, L4left, L4right, mask, np1, np2,
       np3, ptr, r1, r2, S1NG0, S1NG1, S1NG2, S1NG3, S1NG4, S1NG5, S1NG6, S1NG7, S1NG8, S1NG9, S1NG10,
       S1NG11, S1NG12, S1NG13, S1NG14, S1NG15, S1NG16, S1NG17, S1NG18, S1NG19, S1NG20, S1NG21, S1NG22,
       S1NG23, S1NG24, S1NG25, S1NG26, S1NG27, S1NG28, S1NG29, S1NG30, S1NG31, screen_control_1_addr_pass,
       screen_control_1_mask_2, screen_control_1_next_pos, screen_control_1_str0, screen_control_1_str1,
       screen_control_1_str2, screen_control_1_str3, screen_control_1_str4, screen_control_1_str5,
       screen_control_1_str6, screen_control_1_str7, screen_control_1_str8, screen_control_1_str9,
       screen_control_1_str10, screen_control_1_str11, screen_control_1_str12, screen_control_1_str13,
       screen_control_1_str14, screen_control_1_str15, screen_control_1_str16, screen_control_1_str17,
       screen_control_1_str18, screen_control_1_str19, screen_control_1_str20, screen_control_1_str21,
       screen_control_1_str22, screen_control_1_str23, screen_control_1_str24, screen_control_1_str25,
       screen_control_1_str26, screen_control_1_str27, screen_control_1_str28, screen_control_1_str29,
       screen_control_1_str30, screen_control_1_str31, screen_control_1_str_left_out,
       screen_control_1_str_right_out, screen_control_2_addr_pass, screen_control_2_mask_2,
       screen_control_2_next_pos, screen_control_2_str0, screen_control_2_str1, screen_control_2_str2,
       screen_control_2_str3, screen_control_2_str4, screen_control_2_str5, screen_control_2_str6,
       screen_control_2_str7, screen_control_2_str8, screen_control_2_str9, screen_control_2_str10,
       screen_control_2_str11, screen_control_2_str12, screen_control_2_str13, screen_control_2_str14,
       screen_control_2_str15, screen_control_2_str16, screen_control_2_str17, screen_control_2_str18,
       screen_control_2_str19, screen_control_2_str20, screen_control_2_str21, screen_control_2_str22,
       screen_control_2_str23, screen_control_2_str24, screen_control_2_str25, screen_control_2_str26,
       screen_control_2_str27, screen_control_2_str28, screen_control_2_str29, screen_control_2_str30,
       screen_control_2_str31, screen_control_2_str_left_out, screen_control_2_str_right_out,
       screen_control_3_addr_pass, screen_control_3_mask_2, screen_control_3_next_pos, screen_control_3_str0,
       screen_control_3_str1, screen_control_3_str2, screen_control_3_str3, screen_control_3_str4,
       screen_control_3_str5, screen_control_3_str6, screen_control_3_str7, screen_control_3_str8,
       screen_control_3_str9, screen_control_3_str10, screen_control_3_str11, screen_control_3_str12,
       screen_control_3_str13, screen_control_3_str14, screen_control_3_str15, screen_control_3_str16,
       screen_control_3_str17, screen_control_3_str18, screen_control_3_str19, screen_control_3_str20,
       screen_control_3_str21, screen_control_3_str22, screen_control_3_str23, screen_control_3_str24,
       screen_control_3_str25, screen_control_3_str26, screen_control_3_str27, screen_control_3_str28,
       screen_control_3_str29, screen_control_3_str30, screen_control_3_str31, screen_control_3_str_left_out,
       screen_control_3_str_right_out, screen_control_4_addr_pass, screen_control_4_mask_2,
       screen_control_4_next_pos, screen_control_4_str0, screen_control_4_str1, screen_control_4_str2,
       screen_control_4_str3, screen_control_4_str4, screen_control_4_str5, screen_control_4_str6,
       screen_control_4_str7, screen_control_4_str8, screen_control_4_str9, screen_control_4_str10,
       screen_control_4_str11, screen_control_4_str12, screen_control_4_str13, screen_control_4_str14,
       screen_control_4_str15, screen_control_4_str16, screen_control_4_str17, screen_control_4_str18,
       screen_control_4_str19, screen_control_4_str20, screen_control_4_str21, screen_control_4_str22,
       screen_control_4_str23, screen_control_4_str24, screen_control_4_str25, screen_control_4_str26,
       screen_control_4_str27, screen_control_4_str28, screen_control_4_str29, screen_control_4_str30,
       screen_control_4_str31, screen_control_4_str_left_out, screen_control_4_str_right_out,
       screen_control_5_str0, screen_control_5_str1, screen_control_5_str2, screen_control_5_str3,
       screen_control_5_str4, screen_control_5_str5, screen_control_5_str6, screen_control_5_str7,
       screen_control_5_str8, screen_control_5_str9, screen_control_5_str10, screen_control_5_str11,
       screen_control_5_str12, screen_control_5_str13, screen_control_5_str14, screen_control_5_str15,
       screen_control_5_str16, screen_control_5_str17, screen_control_5_str18, screen_control_5_str19,
       screen_control_5_str20, screen_control_5_str21, screen_control_5_str22, screen_control_5_str23,
       screen_control_5_str24, screen_control_5_str25, screen_control_5_str26, screen_control_5_str27,
       screen_control_5_str28, screen_control_5_str29, screen_control_5_str30, screen_control_5_str31,
       screen_control_6_str0, screen_control_6_str1, screen_control_6_str2, screen_control_6_str3,
       screen_control_6_str4, screen_control_6_str5, screen_control_6_str6, screen_control_6_str7,
       screen_control_6_str8, screen_control_6_str9, screen_control_6_str10, screen_control_6_str11,
       screen_control_6_str12, screen_control_6_str13, screen_control_6_str14, screen_control_6_str15,
       screen_control_6_str16, screen_control_6_str17, screen_control_6_str18, screen_control_6_str19,
       screen_control_6_str20, screen_control_6_str21, screen_control_6_str22, screen_control_6_str23,
       screen_control_6_str24, screen_control_6_str25, screen_control_6_str26, screen_control_6_str27,
       screen_control_6_str28, screen_control_6_str29, screen_control_6_str30, screen_control_6_str31,
       screen_control_7_str0, screen_control_7_str1, screen_control_7_str2, screen_control_7_str3,
       screen_control_7_str4, screen_control_7_str5, screen_control_7_str6, screen_control_7_str7,
       screen_control_7_str8, screen_control_7_str9, screen_control_7_str10, screen_control_7_str11,
       screen_control_7_str12, screen_control_7_str13, screen_control_7_str14, screen_control_7_str15,
       screen_control_7_str16, screen_control_7_str17, screen_control_7_str18, screen_control_7_str19,
       screen_control_7_str20, screen_control_7_str21, screen_control_7_str22, screen_control_7_str23,
       screen_control_7_str24, screen_control_7_str25, screen_control_7_str26, screen_control_7_str27,
       screen_control_7_str28, screen_control_7_str29, screen_control_7_str30, screen_control_7_str31,
       screen_control_8_str0, screen_control_8_str1, screen_control_8_str2, screen_control_8_str3,
       screen_control_8_str4, screen_control_8_str5, screen_control_8_str6, screen_control_8_str7,
       screen_control_8_str8, screen_control_8_str9, screen_control_8_str10, screen_control_8_str11,
       screen_control_8_str12, screen_control_8_str13, screen_control_8_str14, screen_control_8_str15,
       screen_control_8_str16, screen_control_8_str17, screen_control_8_str18, screen_control_8_str19,
       screen_control_8_str20, screen_control_8_str21, screen_control_8_str22, screen_control_8_str23,
       screen_control_8_str24, screen_control_8_str25, screen_control_8_str26, screen_control_8_str27,
       screen_control_8_str28, screen_control_8_str29, screen_control_8_str30, screen_control_8_str31;
  wire [31:0] C1DU1_2, C1DU2_3, C1DU3_4, C1DU4_1, C1UD1_4, C1UD2_1, C1UD3_2, C1UD4_3, C2DU1_2, C2DU2_3,
       C2DU3_4, C2DU4_1, C2UD1_4, C2UD2_1, C2UD3_2, C2UD4_3;

  DotMatrix #(.matrixcols(32), .matrixrows(16)) dotmatrix_1 (
    .col0(S1NG0), .col1(S1NG1), .col2(S1NG2), .col3(S1NG3), .col4(S1NG4), .col5(S1NG5), .col6(S1NG6),
    .col7(S1NG7), .col8(S1NG8), .col9(S1NG9), .col10(S1NG10), .col11(S1NG11), .col12(S1NG12), .col13(S1NG13),
    .col14(S1NG14), .col15(S1NG15), .col16(S1NG16), .col17(S1NG17), .col18(S1NG18), .col19(S1NG19),
    .col20(S1NG20), .col21(S1NG21), .col22(S1NG22), .col23(S1NG23), .col24(S1NG24), .col25(S1NG25),
    .col26(S1NG26), .col27(S1NG27), .col28(S1NG28), .col29(S1NG29), .col30(S1NG30), .col31(S1NG31));
  // Probe on cdm16_1_p5
  // Probe on cdm16_1_p5
  // Probe on cdm16_1_p5
  Clock clock_1 (.out(cl));
  and and_1 (ld, read, not_1_out);
  not not_1 (not_1_out, comparator_1_eq);
  Comparator #(.width(16)) comparator_1 (.a(addr), .b(16'hfff0), .eq(comparator_1_eq));  // open: gt, lt
  Comparator #(.width(16)) comparator_2 (.a(r2), .b(16'h8000), .eq(set_col));  // open: gt, lt
  or or_1 (or_1_out, cslrn[4], life_on_mark);
  // Probe on cdm16_1_p5
  // Probe on r1
  // Probe on r1
  // Probe on r1
  but_control but_control_1 (
    .IRQ(but_control_1_irq), .IAck(cdm16_1_p3), .down(down), .left(left), .right(right), .up(up), .clock(cl),
    .life_on(cslrn[2]), .data(data), .addr(addr), .read(read), .vec(vec), .rst(cslrn[3]), .plane(plane),
    .bashni(bashni));
  T_Flip_Flop t_ff_1 (.clk(cl), .T(or_1_out), .Q(_0), .Qn(t_ff_1_qn), .reset(cslrn[3]));  // open: preset, en
  // Probe on r2
  // Probe on r2
  // Probe on r2
  // cdm16 cdm16_1: pin names not known; wires that end beside it: but_control_1_irq, vec, cdm16_1_p3, Hold, cdm16_1_p5, r1, cl, r2, cdm16_1_p9, mask, ptr, cdm16_1_p12, cdm16_1_p13, cdm16_1_p14, cdm16_1_p15, cdm16_1_p16, mem, read, \bit , addr, cdm16_1_p21, cdm16_1_p22
  LED led_1 (.in(life_on_mark));
  Counter #(.width(1), .max('h1)) counter_1 (.Q(life_on_mark), .clk(cslrn[2]));  // open: load, D, count, carry, clr
  Button v (.out(cslrn[2]));
  Button u_u (.out(cslrn[4]));
  Button _0_o (.out(cslrn[3]));
  Button button_1 (.out(plane));
  T_Flip_Flop t_ff_2 (.clk(t_ff_1_qn), .T(or_1_out), .Q(_1), .Qn(t_ff_2_qn), .reset(cslrn[3]));  // open: preset, en
  // Probe on cdm16_1_p9
  // Probe on cdm16_1_p9
  // Probe on cdm16_1_p9
  not not_2 (not_2_out, read);
  assign cdm16_1_p22 = read ? data : 16'bz;  // Controlled_Buffer controlled_buffer_1
  Button button_2 (.out(up));
  Button button_3 (.out(left));
  Button button_4 (.out(right));
  Button v_2 (.out(down));
  Button set (.out(set_op));
  Button button_5 (.out(bashni));
  T_Flip_Flop t_ff_3 (.clk(t_ff_2_qn), .T(or_1_out), .Q(_2), .Qn(t_ff_3_qn), .reset(cslrn[3]));  // open: preset, en
  // Probe on mask
  // Probe on mask
  // Probe on mask
  assign data = not_2_out ? cdm16_1_p21 : 16'bz;  // Controlled_Buffer controlled_buffer_2
  DotMatrix #(.matrixcols(32), .matrixrows(16)) dotmatrix_2 (
    .col0(screen_control_1_str0), .col1(screen_control_1_str1), .col2(screen_control_1_str2),
    .col3(screen_control_1_str3), .col4(screen_control_1_str4), .col5(screen_control_1_str5),
    .col6(screen_control_1_str6), .col7(screen_control_1_str7), .col8(screen_control_1_str8),
    .col9(screen_control_1_str9), .col10(screen_control_1_str10), .col11(screen_control_1_str11),
    .col12(screen_control_1_str12), .col13(screen_control_1_str13), .col14(screen_control_1_str14),
    .col15(screen_control_1_str15), .col16(screen_control_1_str16), .col17(screen_control_1_str17),
    .col18(screen_control_1_str18), .col19(screen_control_1_str19), .col20(screen_control_1_str20),
    .col21(screen_control_1_str21), .col22(screen_control_1_str22), .col23(screen_control_1_str23),
    .col24(screen_control_1_str24), .col25(screen_control_1_str25), .col26(screen_control_1_str26),
    .col27(screen_control_1_str27), .col28(screen_control_1_str28), .col29(screen_control_1_str29),
    .col30(screen_control_1_str30), .col31(screen_control_1_str31));
  DotMatrix #(.matrixcols(32), .matrixrows(16)) dotmatrix_3 (
    .col0(screen_control_2_str0), .col1(screen_control_2_str1), .col2(screen_control_2_str2),
    .col3(screen_control_2_str3), .col4(screen_control_2_str4), .col5(screen_control_2_str5),
    .col6(screen_control_2_str6), .col7(screen_control_2_str7), .col8(screen_control_2_str8),
    .col9(screen_control_2_str9), .col10(screen_control_2_str10), .col11(screen_control_2_str11),
    .col12(screen_control_2_str12), .col13(screen_control_2_str13), .col14(screen_control_2_str14),
    .col15(screen_control_2_str15), .col16(screen_control_2_str16), .col17(screen_control_2_str17),
    .col18(screen_control_2_str18), .col19(screen_control_2_str19), .col20(screen_control_2_str20),
    .col21(screen_control_2_str21), .col22(screen_control_2_str22), .col23(screen_control_2_str23),
    .col24(screen_control_2_str24), .col25(screen_control_2_str25), .col26(screen_control_2_str26),
    .col27(screen_control_2_str27), .col28(screen_control_2_str28), .col29(screen_control_2_str29),
    .col30(screen_control_2_str30), .col31(screen_control_2_str31));
  DotMatrix #(.matrixcols(32), .matrixrows(16)) dotmatrix_4 (
    .col0(screen_control_3_str0), .col1(screen_control_3_str1), .col2(screen_control_3_str2),
    .col3(screen_control_3_str3), .col4(screen_control_3_str4), .col5(screen_control_3_str5),
    .col6(screen_control_3_str6), .col7(screen_control_3_str7), .col8(screen_control_3_str8),
    .col9(screen_control_3_str9), .col10(screen_control_3_str10), .col11(screen_control_3_str11),
    .col12(screen_control_3_str12), .col13(screen_control_3_str13), .col14(screen_control_3_str14),
    .col15(screen_control_3_str15), .col16(screen_control_3_str16), .col17(screen_control_3_str17),
    .col18(screen_control_3_str18), .col19(screen_control_3_str19), .col20(screen_control_3_str20),
    .col21(screen_control_3_str21), .col22(screen_control_3_str22), .col23(screen_control_3_str23),
    .col24(screen_control_3_str24), .col25(screen_control_3_str25), .col26(screen_control_3_str26),
    .col27(screen_control_3_str27), .col28(screen_control_3_str28), .col29(screen_control_3_str29),
    .col30(screen_control_3_str30), .col31(screen_control_3_str31));
  DotMatrix #(.matrixcols(32), .matrixrows(16)) dotmatrix_5 (
    .col0(screen_control_4_str0), .col1(screen_control_4_str1), .col2(screen_control_4_str2),
    .col3(screen_control_4_str3), .col4(screen_control_4_str4), .col5(screen_control_4_str5),
    .col6(screen_control_4_str6), .col7(screen_control_4_str7), .col8(screen_control_4_str8),
    .col9(screen_control_4_str9), .col10(screen_control_4_str10), .col11(screen_control_4_str11),
    .col12(screen_control_4_str12), .col13(screen_control_4_str13), .col14(screen_control_4_str14),
    .col15(screen_control_4_str15), .col16(screen_control_4_str16), .col17(screen_control_4_str17),
    .col18(screen_control_4_str18), .col19(screen_control_4_str19), .col20(screen_control_4_str20),
    .col21(screen_control_4_str21), .col22(screen_control_4_str22), .col23(screen_control_4_str23),
    .col24(screen_control_4_str24), .col25(screen_control_4_str25), .col26(screen_control_4_str26),
    .col27(screen_control_4_str27), .col28(screen_control_4_str28), .col29(screen_control_4_str29),
    .col30(screen_control_4_str30), .col31(screen_control_4_str31));
  T_Flip_Flop t_ff_4 (.clk(t_ff_3_qn), .T(or_1_out), .Q(_3), .Qn(t_ff_4_qn), .reset(cslrn[3]));  // open: preset, en
  // Probe on mask
  // Probe on ptr
  // Probe on ptr
  // Probe on ptr
  // Probe on data
  // Probe on data
  // Probe on data
  // Probe on data
  T_Flip_Flop t_ff_5 (.clk(t_ff_4_qn), .T(or_1_out), .Q(_4), .Qn(t_ff_5_qn), .reset(cslrn[3]));  // open: preset, en
  // Probe on cdm16_1_p12
  // Probe on cdm16_1_p12
  // Probe on cdm16_1_p12
  // Probe on addr
  // Probe on addr
  // Probe on addr
  // Probe on addr
  screen_control screen_control_1 (
    .addr(ptr), .start_pos({16{1'b0}}), .next_pos(screen_control_1_next_pos),
    .addr_pass(screen_control_1_addr_pass), .str_up_out(C1UD1_4), .str_down_out(C1DU1_2),
    .str_up_in(C1DU4_1), .str_down_in(C1UD2_1), .str_right_out(screen_control_1_str_right_out),
    .str_left_out(screen_control_1_str_left_out), .str_right_in(L1right), .str_left_in(L1left),
    .corners_in(CR1IN), .corners_out(CR1OUT), .next_gen_0(S1NG0), .next_gen_1(S1NG1), .next_gen_2(S1NG2),
    .next_gen_3(S1NG3), .next_gen_4(S1NG4), .next_gen_5(S1NG5), .next_gen_6(S1NG6), .next_gen_7(S1NG7),
    .next_gen_8(S1NG8), .next_gen_9(S1NG9), .next_gen_10(S1NG10), .next_gen_11(S1NG11), .next_gen_12(S1NG12),
    .next_gen_13(S1NG13), .next_gen_14(S1NG14), .next_gen_15(S1NG15), .next_gen_16(S1NG16),
    .next_gen_17(S1NG17), .next_gen_18(S1NG18), .next_gen_19(S1NG19), .next_gen_20(S1NG20),
    .next_gen_21(S1NG21), .next_gen_22(S1NG22), .next_gen_23(S1NG23), .next_gen_24(S1NG24),
    .next_gen_25(S1NG25), .next_gen_26(S1NG26), .next_gen_27(S1NG27), .next_gen_28(S1NG28),
    .next_gen_29(S1NG29), .next_gen_30(S1NG30), .next_gen_31(S1NG31), .str16(screen_control_1_str16),
    .str17(screen_control_1_str17), .str18(screen_control_1_str18), .str19(screen_control_1_str19),
    .str20(screen_control_1_str20), .str21(screen_control_1_str21), .str22(screen_control_1_str22),
    .str23(screen_control_1_str23), .str24(screen_control_1_str24), .str25(screen_control_1_str25),
    .str26(screen_control_1_str26), .str27(screen_control_1_str27), .str28(screen_control_1_str28),
    .str29(screen_control_1_str29), .str30(screen_control_1_str30), .str31(screen_control_1_str31),
    .str0(screen_control_1_str0), .str1(screen_control_1_str1), .str2(screen_control_1_str2),
    .str3(screen_control_1_str3), .str4(screen_control_1_str4), .str5(screen_control_1_str5),
    .str6(screen_control_1_str6), .str7(screen_control_1_str7), .str8(screen_control_1_str8),
    .str9(screen_control_1_str9), .str10(screen_control_1_str10), .str11(screen_control_1_str11),
    .str12(screen_control_1_str12), .str13(screen_control_1_str13), .str14(screen_control_1_str14),
    .str15(screen_control_1_str15), .cslr({cslrn, cl}), .mask(mask), .cslr_2(screen_control_1_cslr_2),
    .mask_2(screen_control_1_mask_2));
  screen_control screen_control_2 (
    .addr(ptr), .start_pos(np1), .next_pos(screen_control_2_next_pos),
    .addr_pass(screen_control_2_addr_pass), .str_up_out(C1UD2_1), .str_down_out(C1DU2_3),
    .str_up_in(C1DU1_2), .str_down_in(C1UD3_2), .str_right_out(screen_control_2_str_right_out),
    .str_left_out(screen_control_2_str_left_out), .str_right_in(L2right), .str_left_in(L2left),
    .corners_in({CR2OUT[1], CR3IN, CR2OUT[2]}), .corners_out({CR2IN[1], CR3OUT, CR2IN[2]}),
    .str16(screen_control_2_str16), .str17(screen_control_2_str17), .str18(screen_control_2_str18),
    .str19(screen_control_2_str19), .str20(screen_control_2_str20), .str21(screen_control_2_str21),
    .str22(screen_control_2_str22), .str23(screen_control_2_str23), .str24(screen_control_2_str24),
    .str25(screen_control_2_str25), .str26(screen_control_2_str26), .str27(screen_control_2_str27),
    .str28(screen_control_2_str28), .str29(screen_control_2_str29), .str30(screen_control_2_str30),
    .str31(screen_control_2_str31), .str0(screen_control_2_str0), .str1(screen_control_2_str1),
    .str2(screen_control_2_str2), .str3(screen_control_2_str3), .str4(screen_control_2_str4),
    .str5(screen_control_2_str5), .str6(screen_control_2_str6), .str7(screen_control_2_str7),
    .str8(screen_control_2_str8), .str9(screen_control_2_str9), .str10(screen_control_2_str10),
    .str11(screen_control_2_str11), .str12(screen_control_2_str12), .str13(screen_control_2_str13),
    .str14(screen_control_2_str14), .str15(screen_control_2_str15), .cslr({cslrn, cl}), .mask(mask),
    .cslr_2(screen_control_2_cslr_2), .mask_2(screen_control_2_mask_2));  // open: next_gen_0, next_gen_1, next_gen_2, next_gen_3, next_gen_4, next_gen_5, next_gen_6, next_gen_7, next_gen_8, next_gen_9, next_gen_10, next_gen_11, next_gen_12, next_gen_13, next_gen_14, next_gen_15, next_gen_16, next_gen_17, next_gen_18, next_gen_19, next_gen_20, next_gen_21, next_gen_22, next_gen_23, next_gen_24, next_gen_25, next_gen_26, next_gen_27, next_gen_28, next_gen_29, next_gen_30, next_gen_31
  screen_control screen_control_3 (
    .addr(ptr), .start_pos(np2), .next_pos(screen_control_3_next_pos),
    .addr_pass(screen_control_3_addr_pass), .str_up_out(C1UD3_2), .str_down_out(C1DU3_4),
    .str_up_in(C1DU2_3), .str_down_in(C1UD4_3), .str_right_out(screen_control_3_str_right_out),
    .str_left_out(screen_control_3_str_left_out), .str_right_in(L3right), .str_left_in(L3left),
    .corners_in({CR4OUT[1], CR5IN, CR4OUT[2]}), .corners_out({CR4IN[1], CR5OUT, CR4IN[2]}),
    .str16(screen_control_3_str16), .str17(screen_control_3_str17), .str18(screen_control_3_str18),
    .str19(screen_control_3_str19), .str20(screen_control_3_str20), .str21(screen_control_3_str21),
    .str22(screen_control_3_str22), .str23(screen_control_3_str23), .str24(screen_control_3_str24),
    .str25(screen_control_3_str25), .str26(screen_control_3_str26), .str27(screen_control_3_str27),
    .str28(screen_control_3_str28), .str29(screen_control_3_str29), .str30(screen_control_3_str30),
    .str31(screen_control_3_str31), .str0(screen_control_3_str0), .str1(screen_control_3_str1),
    .str2(screen_control_3_str2), .str3(screen_control_3_str3), .str4(screen_control_3_str4),
    .str5(screen_control_3_str5), .str6(screen_control_3_str6), .str7(screen_control_3_str7),
    .str8(screen_control_3_str8), .str9(screen_control_3_str9), .str10(screen_control_3_str10),
    .str11(screen_control_3_str11), .str12(screen_control_3_str12), .str13(screen_control_3_str13),
    .str14(screen_control_3_str14), .str15(screen_control_3_str15), .cslr({cslrn, cl}), .mask(mask),
    .cslr_2(screen_control_3_cslr_2), .mask_2(screen_control_3_mask_2));  // open: next_gen_0, next_gen_1, next_gen_2, next_gen_3, next_gen_4, next_gen_5, next_gen_6, next_gen_7, next_gen_8, next_gen_9, next_gen_10, next_gen_11, next_gen_12, next_gen_13, next_gen_14, next_gen_15, next_gen_16, next_gen_17, next_gen_18, next_gen_19, next_gen_20, next_gen_21, next_gen_22, next_gen_23, next_gen_24, next_gen_25, next_gen_26, next_gen_27, next_gen_28, next_gen_29, next_gen_30, next_gen_31
  screen_control screen_control_4 (
    .addr(ptr), .start_pos(np3), .next_pos(screen_control_4_next_pos),
    .addr_pass(screen_control_4_addr_pass), .str_up_out(C1UD4_3), .str_down_out(C1DU4_1),
    .str_up_in(C1DU3_4), .str_down_in(C1UD1_4), .str_right_out(screen_control_4_str_right_out),
    .str_left_out(screen_control_4_str_left_out), .str_right_in(L4right), .str_left_in(L4left),
    .corners_in({CR6OUT[1], CR2OUT[0], CR2OUT[3], CR6OUT[2]}),
    .corners_out({CR6IN[1], CR2IN[0], CR2IN[3], CR6IN[2]}), .str16(screen_control_4_str16),
    .str17(screen_control_4_str17), .str18(screen_control_4_str18), .str19(screen_control_4_str19),
    .str20(screen_control_4_str20), .str21(screen_control_4_str21), .str22(screen_control_4_str22),
    .str23(screen_control_4_str23), .str24(screen_control_4_str24), .str25(screen_control_4_str25),
    .str26(screen_control_4_str26), .str27(screen_control_4_str27), .str28(screen_control_4_str28),
    .str29(screen_control_4_str29), .str30(screen_control_4_str30), .str31(screen_control_4_str31),
    .str0(screen_control_4_str0), .str1(screen_control_4_str1), .str2(screen_control_4_str2),
    .str3(screen_control_4_str3), .str4(screen_control_4_str4), .str5(screen_control_4_str5),
    .str6(screen_control_4_str6), .str7(screen_control_4_str7), .str8(screen_control_4_str8),
    .str9(screen_control_4_str9), .str10(screen_control_4_str10), .str11(screen_control_4_str11),
    .str12(screen_control_4_str12), .str13(screen_control_4_str13), .str14(screen_control_4_str14),
    .str15(screen_control_4_str15), .cslr({cslrn, cl}), .mask(mask), .cslr_2(screen_control_4_cslr_2),
    .mask_2(screen_control_4_mask_2));  // open: next_gen_0, next_gen_1, next_gen_2, next_gen_3, next_gen_4, next_gen_5, next_gen_6, next_gen_7, next_gen_8, next_gen_9, next_gen_10, next_gen_11, next_gen_12, next_gen_13, next_gen_14, next_gen_15, next_gen_16, next_gen_17, next_gen_18, next_gen_19, next_gen_20, next_gen_21, next_gen_22, next_gen_23, next_gen_24, next_gen_25, next_gen_26, next_gen_27, next_gen_28, next_gen_29, next_gen_30, next_gen_31
  T_Flip_Flop t_ff_6 (.clk(t_ff_5_qn), .T(or_1_out), .Q(_5), .Qn(t_ff_6_qn), .reset(cslrn[3]));  // open: preset, en
  // Probe on cdm16_1_p13
  // Probe on cdm16_1_p13
  // Probe on cdm16_1_p13
  // RAM ram_1: pin names not known; wires that end beside it: addr, \bit , mem, cl, ld, data
  T_Flip_Flop t_ff_7 (.clk(t_ff_6_qn), .T(or_1_out), .Q(_6), .Qn(t_ff_7_qn), .reset(cslrn[3]));  // open: preset, en
  // Probe on cdm16_1_p14
  // Probe on cdm16_1_p14
  // Probe on cdm16_1_p14
  // Debugger debugger_1: pin names not known
  DotMatrix #(.matrixcols(32), .matrixrows(16)) dotmatrix_6 (
    .col0(screen_control_5_str0), .col1(screen_control_5_str1), .col2(screen_control_5_str2),
    .col3(screen_control_5_str3), .col4(screen_control_5_str4), .col5(screen_control_5_str5),
    .col6(screen_control_5_str6), .col7(screen_control_5_str7), .col8(screen_control_5_str8),
    .col9(screen_control_5_str9), .col10(screen_control_5_str10), .col11(screen_control_5_str11),
    .col12(screen_control_5_str12), .col13(screen_control_5_str13), .col14(screen_control_5_str14),
    .col15(screen_control_5_str15), .col16(screen_control_5_str16), .col17(screen_control_5_str17),
    .col18(screen_control_5_str18), .col19(screen_control_5_str19), .col20(screen_control_5_str20),
    .col21(screen_control_5_str21), .col22(screen_control_5_str22), .col23(screen_control_5_str23),
    .col24(screen_control_5_str24), .col25(screen_control_5_str25), .col26(screen_control_5_str26),
    .col27(screen_control_5_str27), .col28(screen_control_5_str28), .col29(screen_control_5_str29),
    .col30(screen_control_5_str30), .col31(screen_control_5_str31));
  DotMatrix #(.matrixcols(32), .matrixrows(16)) dotmatrix_7 (
    .col0(screen_control_6_str0), .col1(screen_control_6_str1), .col2(screen_control_6_str2),
    .col3(screen_control_6_str3), .col4(screen_control_6_str4), .col5(screen_control_6_str5),
    .col6(screen_control_6_str6), .col7(screen_control_6_str7), .col8(screen_control_6_str8),
    .col9(screen_control_6_str9), .col10(screen_control_6_str10), .col11(screen_control_6_str11),
    .col12(screen_control_6_str12), .col13(screen_control_6_str13), .col14(screen_control_6_str14),
    .col15(screen_control_6_str15), .col16(screen_control_6_str16), .col17(screen_control_6_str17),
    .col18(screen_control_6_str18), .col19(screen_control_6_str19), .col20(screen_control_6_str20),
    .col21(screen_control_6_str21), .col22(screen_control_6_str22), .col23(screen_control_6_str23),
    .col24(screen_control_6_str24), .col25(screen_control_6_str25), .col26(screen_control_6_str26),
    .col27(screen_control_6_str27), .col28(screen_control_6_str28), .col29(screen_control_6_str29),
    .col30(screen_control_6_str30), .col31(screen_control_6_str31));
  DotMatrix #(.matrixcols(32), .matrixrows(16)) dotmatrix_8 (
    .col0(screen_control_7_str0), .col1(screen_control_7_str1), .col2(screen_control_7_str2),
    .col3(screen_control_7_str3), .col4(screen_control_7_str4), .col5(screen_control_7_str5),
    .col6(screen_control_7_str6), .col7(screen_control_7_str7), .col8(screen_control_7_str8),
    .col9(screen_control_7_str9), .col10(screen_control_7_str10), .col11(screen_control_7_str11),
    .col12(screen_control_7_str12), .col13(screen_control_7_str13), .col14(screen_control_7_str14),
    .col15(screen_control_7_str15), .col16(screen_control_7_str16), .col17(screen_control_7_str17),
    .col18(screen_control_7_str18), .col19(screen_control_7_str19), .col20(screen_control_7_str20),
    .col21(screen_control_7_str21), .col22(screen_control_7_str22), .col23(screen_control_7_str23),
    .col24(screen_control_7_str24), .col25(screen_control_7_str25), .col26(screen_control_7_str26),
    .col27(screen_control_7_str27), .col28(screen_control_7_str28), .col29(screen_control_7_str29),
    .col30(screen_control_7_str30), .col31(screen_control_7_str31));
  DotMatrix #(.matrixcols(32), .matrixrows(16)) dotmatrix_9 (
    .col0(screen_control_8_str0), .col1(screen_control_8_str1), .col2(screen_control_8_str2),
    .col3(screen_control_8_str3), .col4(screen_control_8_str4), .col5(screen_control_8_str5),
    .col6(screen_control_8_str6), .col7(screen_control_8_str7), .col8(screen_control_8_str8),
    .col9(screen_control_8_str9), .col10(screen_control_8_str10), .col11(screen_control_8_str11),
    .col12(screen_control_8_str12), .col13(screen_control_8_str13), .col14(screen_control_8_str14),
    .col15(screen_control_8_str15), .col16(screen_control_8_str16), .col17(screen_control_8_str17),
    .col18(screen_control_8_str18), .col19(screen_control_8_str19), .col20(screen_control_8_str20),
    .col21(screen_control_8_str21), .col22(screen_control_8_str22), .col23(screen_control_8_str23),
    .col24(screen_control_8_str24), .col25(screen_control_8_str25), .col26(screen_control_8_str26),
    .col27(screen_control_8_str27), .col28(screen_control_8_str28), .col29(screen_control_8_str29),
    .col30(screen_control_8_str30), .col31(screen_control_8_str31));
  T_Flip_Flop t_ff_8 (.clk(t_ff_7_qn), .T(or_1_out), .Q(_7), .Qn(t_ff_8_qn), .reset(cslrn[3]));  // open: preset, en
  // Probe on cdm16_1_p15
  // Probe on cdm16_1_p15
  // Probe on cdm16_1_p15
  T_Flip_Flop t_ff_9 (.clk(t_ff_8_qn), .T(or_1_out), .Q(_8), .Qn(t_ff_9_qn), .reset(cslrn[3]));  // open: preset, en
  // Probe on cdm16_1_p16
  // Probe on cdm16_1_p16
  // Probe on cdm16_1_p16
  or or_2 (cslrn[1], set_col, set_op);
  screen_control screen_control_5 (
    .addr(screen_control_1_addr_pass), .start_pos(screen_control_1_next_pos), .next_pos(np1),
    .str_up_out(C2UD1_4), .str_down_out(C2DU1_2), .str_up_in(C2DU4_1), .str_down_in(C2UD2_1),
    .str_right_out(L1left), .str_left_out(L1right), .str_right_in(screen_control_1_str_left_out),
    .str_left_in(screen_control_1_str_right_out), .corners_in(CR2IN), .corners_out(CR2OUT),
    .str16(screen_control_5_str16), .str17(screen_control_5_str17), .str18(screen_control_5_str18),
    .str19(screen_control_5_str19), .str20(screen_control_5_str20), .str21(screen_control_5_str21),
    .str22(screen_control_5_str22), .str23(screen_control_5_str23), .str24(screen_control_5_str24),
    .str25(screen_control_5_str25), .str26(screen_control_5_str26), .str27(screen_control_5_str27),
    .str28(screen_control_5_str28), .str29(screen_control_5_str29), .str30(screen_control_5_str30),
    .str31(screen_control_5_str31), .str0(screen_control_5_str0), .str1(screen_control_5_str1),
    .str2(screen_control_5_str2), .str3(screen_control_5_str3), .str4(screen_control_5_str4),
    .str5(screen_control_5_str5), .str6(screen_control_5_str6), .str7(screen_control_5_str7),
    .str8(screen_control_5_str8), .str9(screen_control_5_str9), .str10(screen_control_5_str10),
    .str11(screen_control_5_str11), .str12(screen_control_5_str12), .str13(screen_control_5_str13),
    .str14(screen_control_5_str14), .str15(screen_control_5_str15), .cslr(screen_control_1_cslr_2),
    .mask(screen_control_1_mask_2));  // open: addr_pass, next_gen_0, next_gen_1, next_gen_2, next_gen_3, next_gen_4, next_gen_5, next_gen_6, next_gen_7, next_gen_8, next_gen_9, next_gen_10, next_gen_11, next_gen_12, next_gen_13, next_gen_14, next_gen_15, next_gen_16, next_gen_17, next_gen_18, next_gen_19, next_gen_20, next_gen_21, next_gen_22, next_gen_23, next_gen_24, next_gen_25, next_gen_26, next_gen_27, next_gen_28, next_gen_29, next_gen_30, next_gen_31, cslr_2, mask_2
  screen_control screen_control_6 (
    .addr(screen_control_2_addr_pass), .start_pos(screen_control_2_next_pos), .next_pos(np2),
    .str_up_out(C2UD2_1), .str_down_out(C2DU2_3), .str_up_in(C2DU1_2), .str_down_in(C2UD3_2),
    .str_right_out(L2left), .str_left_out(L2right), .str_right_in(screen_control_2_str_left_out),
    .str_left_in(screen_control_2_str_right_out), .corners_in({CR1OUT[1], CR4IN, CR1OUT[2]}),
    .corners_out({CR1IN[1], CR4OUT, CR1IN[2]}), .str16(screen_control_6_str16),
    .str17(screen_control_6_str17), .str18(screen_control_6_str18), .str19(screen_control_6_str19),
    .str20(screen_control_6_str20), .str21(screen_control_6_str21), .str22(screen_control_6_str22),
    .str23(screen_control_6_str23), .str24(screen_control_6_str24), .str25(screen_control_6_str25),
    .str26(screen_control_6_str26), .str27(screen_control_6_str27), .str28(screen_control_6_str28),
    .str29(screen_control_6_str29), .str30(screen_control_6_str30), .str31(screen_control_6_str31),
    .str0(screen_control_6_str0), .str1(screen_control_6_str1), .str2(screen_control_6_str2),
    .str3(screen_control_6_str3), .str4(screen_control_6_str4), .str5(screen_control_6_str5),
    .str6(screen_control_6_str6), .str7(screen_control_6_str7), .str8(screen_control_6_str8),
    .str9(screen_control_6_str9), .str10(screen_control_6_str10), .str11(screen_control_6_str11),
    .str12(screen_control_6_str12), .str13(screen_control_6_str13), .str14(screen_control_6_str14),
    .str15(screen_control_6_str15), .cslr(screen_control_2_cslr_2), .mask(screen_control_2_mask_2));  // open: addr_pass, next_gen_0, next_gen_1, next_gen_2, next_gen_3, next_gen_4, next_gen_5, next_gen_6, next_gen_7, next_gen_8, next_gen_9, next_gen_10, next_gen_11, next_gen_12, next_gen_13, next_gen_14, next_gen_15, next_gen_16, next_gen_17, next_gen_18, next_gen_19, next_gen_20, next_gen_21, next_gen_22, next_gen_23, next_gen_24, next_gen_25, next_gen_26, next_gen_27, next_gen_28, next_gen_29, next_gen_30, next_gen_31, cslr_2, mask_2
  screen_control screen_control_7 (
    .addr(screen_control_3_addr_pass), .start_pos(screen_control_3_next_pos), .next_pos(np3),
    .str_up_out(C2UD3_2), .str_down_out(C2DU3_4), .str_up_in(C2DU2_3), .str_down_in(C2UD4_3),
    .str_right_out(L3left), .str_left_out(L3right), .str_right_in(screen_control_3_str_left_out),
    .str_left_in(screen_control_3_str_right_out), .corners_in({CR3OUT[1], CR6IN, CR3OUT[2]}),
    .corners_out({CR3IN[1], CR6OUT, CR3IN[2]}), .str16(screen_control_7_str16),
    .str17(screen_control_7_str17), .str18(screen_control_7_str18), .str19(screen_control_7_str19),
    .str20(screen_control_7_str20), .str21(screen_control_7_str21), .str22(screen_control_7_str22),
    .str23(screen_control_7_str23), .str24(screen_control_7_str24), .str25(screen_control_7_str25),
    .str26(screen_control_7_str26), .str27(screen_control_7_str27), .str28(screen_control_7_str28),
    .str29(screen_control_7_str29), .str30(screen_control_7_str30), .str31(screen_control_7_str31),
    .str0(screen_control_7_str0), .str1(screen_control_7_str1), .str2(screen_control_7_str2),
    .str3(screen_control_7_str3), .str4(screen_control_7_str4), .str5(screen_control_7_str5),
    .str6(screen_control_7_str6), .str7(screen_control_7_str7), .str8(screen_control_7_str8),
    .str9(screen_control_7_str9), .str10(screen_control_7_str10), .str11(screen_control_7_str11),
    .str12(screen_control_7_str12), .str13(screen_control_7_str13), .str14(screen_control_7_str14),
    .str15(screen_control_7_str15), .cslr(screen_control_3_cslr_2), .mask(screen_control_3_mask_2));  // open: addr_pass, next_gen_0, next_gen_1, next_gen_2, next_gen_3, next_gen_4, next_gen_5, next_gen_6, next_gen_7, next_gen_8, next_gen_9, next_gen_10, next_gen_11, next_gen_12, next_gen_13, next_gen_14, next_gen_15, next_gen_16, next_gen_17, next_gen_18, next_gen_19, next_gen_20, next_gen_21, next_gen_22, next_gen_23, next_gen_24, next_gen_25, next_gen_26, next_gen_27, next_gen_28, next_gen_29, next_gen_30, next_gen_31, cslr_2, mask_2
  screen_control screen_control_8 (
    .addr(screen_control_4_addr_pass), .start_pos(screen_control_4_next_pos), .str_up_out(C2UD4_3),
    .str_down_out(C2DU4_1), .str_up_in(C2DU3_4), .str_down_in(C2UD1_4), .str_right_out(L4left),
    .str_left_out(L4right), .str_right_in(screen_control_4_str_left_out),
    .str_left_in(screen_control_4_str_right_out), .corners_in({CR5OUT[1], CR1OUT[0], CR1OUT[3], CR5OUT[2]}),
    .corners_out({CR5IN[1], CR1IN[0], CR1IN[3], CR5IN[2]}), .str16(screen_control_8_str16),
    .str17(screen_control_8_str17), .str18(screen_control_8_str18), .str19(screen_control_8_str19),
    .str20(screen_control_8_str20), .str21(screen_control_8_str21), .str22(screen_control_8_str22),
    .str23(screen_control_8_str23), .str24(screen_control_8_str24), .str25(screen_control_8_str25),
    .str26(screen_control_8_str26), .str27(screen_control_8_str27), .str28(screen_control_8_str28),
    .str29(screen_control_8_str29), .str30(screen_control_8_str30), .str31(screen_control_8_str31),
    .str0(screen_control_8_str0), .str1(screen_control_8_str1), .str2(screen_control_8_str2),
    .str3(screen_control_8_str3), .str4(screen_control_8_str4), .str5(screen_control_8_str5),
    .str6(screen_control_8_str6), .str7(screen_control_8_str7), .str8(screen_control_8_str8),
    .str9(screen_control_8_str9), .str10(screen_control_8_str10), .str11(screen_control_8_str11),
    .str12(screen_control_8_str12), .str13(screen_control_8_str13), .str14(screen_control_8_str14),
    .str15(screen_control_8_str15), .cslr(screen_control_4_cslr_2), .mask(screen_control_4_mask_2));  // open: next_pos, addr_pass, next_gen_0, next_gen_1, next_gen_2, next_gen_3, next_gen_4, next_gen_5, next_gen_6, next_gen_7, next_gen_8, next_gen_9, next_gen_10, next_gen_11, next_gen_12, next_gen_13, next_gen_14, next_gen_15, next_gen_16, next_gen_17, next_gen_18, next_gen_19, next_gen_20, next_gen_21, next_gen_22, next_gen_23, next_gen_24, next_gen_25, next_gen_26, next_gen_27, next_gen_28, next_gen_29, next_gen_30, next_gen_31, cslr_2, mask_2
  T_Flip_Flop t_ff_10 (.clk(t_ff_9_qn), .T(or_1_out), .Q(_9), .Qn(t_ff_10_qn), .reset(cslrn[3]));  // open: preset, en
  // Probe on cdm16_1_p16
  T_Flip_Flop t_ff_11 (.clk(t_ff_10_qn), .T(or_1_out), .Q(_10), .Qn(t_ff_11_qn), .reset(cslrn[3]));  // open: preset, en
  T_Flip_Flop t_ff_12 (.clk(t_ff_11_qn), .T(or_1_out), .Q(_11), .Qn(t_ff_12_qn), .reset(cslrn[3]));  // open: preset, en
  _7_Segment_Display u_7_segment_display_1 (
    .g(hton_2_g), .f(hton_2_f), .a(hton_2_a), .b(hton_2_b), .e(hton_2_e), .d(hton_2_d), .c(hton_2_c));  // open: dp
  _7_Segment_Display u_7_segment_display_2 (
    .g(hton_1_g), .f(hton_1_f), .a(hton_1_a), .b(hton_1_b), .e(hton_1_e), .d(hton_1_d), .c(hton_1_c));  // open: dp
  hton hton_1 (
    .a(hton_1_a), .b(hton_1_b), .c(hton_1_c), .d(hton_1_d), .e(hton_1_e), .f(hton_1_f), .g(hton_1_g),
    .in_1(del_1_thousand));
  hton hton_2 (
    .a(hton_2_a), .b(hton_2_b), .c(hton_2_c), .d(hton_2_d), .e(hton_2_e), .f(hton_2_f), .g(hton_2_g),
    .in_1(del_1_ten_thousand));
  del del_1 (
    .one(del_1_one), .ten(del_1_ten), .hundred(del_1_hundred), .thousand(del_1_thousand),
    .ten_thousand(del_1_ten_thousand),
    .in_1({_15, _14, _13, _12, _11, _10, _9, _8, _7, _6, _5, _4, _3, _2, _1, _0}));
  T_Flip_Flop t_ff_13 (.clk(t_ff_12_qn), .T(or_1_out), .Q(_12), .Qn(t_ff_13_qn), .reset(cslrn[3]));  // open: preset, en
  _7_Segment_Display u_7_segment_display_3 (
    .g(hton_3_g), .f(hton_3_f), .a(hton_3_a), .b(hton_3_b), .e(hton_3_e), .d(hton_3_d), .c(hton_3_c));  // open: dp
  _7_Segment_Display u_7_segment_display_4 (
    .g(hton_4_g), .f(hton_4_f), .a(hton_4_a), .b(hton_4_b), .e(hton_4_e), .d(hton_4_d), .c(hton_4_c));  // open: dp
  hton hton_3 (
    .a(hton_3_a), .b(hton_3_b), .c(hton_3_c), .d(hton_3_d), .e(hton_3_e), .f(hton_3_f), .g(hton_3_g),
    .in_1(del_1_ten));
  hton hton_4 (
    .a(hton_4_a), .b(hton_4_b), .c(hton_4_c), .d(hton_4_d), .e(hton_4_e), .f(hton_4_f), .g(hton_4_g),
    .in_1(del_1_hundred));
  T_Flip_Flop t_ff_14 (.clk(t_ff_13_qn), .T(or_1_out), .Q(_13), .Qn(t_ff_14_qn), .reset(cslrn[3]));  // open: preset, en
  _7_Segment_Display u_7_segment_display_5 (
    .g(hton_5_g), .f(hton_5_f), .a(hton_5_a), .b(hton_5_b), .e(hton_5_e), .d(hton_5_d), .c(hton_5_c));  // open: dp
  hton hton_5 (
    .a(hton_5_a), .b(hton_5_b), .c(hton_5_c), .d(hton_5_d), .e(hton_5_e), .f(hton_5_f), .g(hton_5_g),
    .in_1(del_1_one));
  T_Flip_Flop t_ff_15 (.clk(t_ff_14_qn), .T(or_1_out), .Q(_14), .Qn(t_ff_15_qn), .reset(cslrn[3]));  // open: preset, en
  T_Flip_Flop t_ff_16 (.clk(t_ff_15_qn), .T(or_1_out), .Q(_15), .reset(cslrn[3]));  // open: Qn, preset, en

  // Other names for the same wires on the sheet: CR7IN[3:0] = {CR6OUT[1], CR2OUT[0], CR2OUT[3], CR6OUT[2]};
  //   CR3IN (some bits) = {CR2OUT[1], CR2OUT[2]}; CR3OUT (some bits) = {CR2IN[1], CR2IN[2]};
  //   CR6IN (some bits) = {CR3OUT[1], CR3OUT[2]}; CR4IN (some bits) = {CR1OUT[1], CR1OUT[2]};
  //   CR4OUT (some bits) = {CR1IN[1], CR1IN[2]}; CR5IN (some bits) = {CR4OUT[1], CR4OUT[2]};
  //   CR5OUT (some bits) = {CR4IN[1], CR4IN[2]}; CR8IN[3:0] = {CR5OUT[1], CR1OUT[0], CR1OUT[3], CR5OUT[2]};
  //   CR6OUT (some bits) = {CR3IN[1], CR3IN[2]}; CR7OUT[3:0] = {CR6IN[1], CR2IN[0], CR2IN[3], CR6IN[2]};
  //   CR8OUT[3:0] = {CR5IN[1], CR1IN[0], CR1IN[3], CR5IN[2]}; cslrn[0] = cl; life_on = cslrn[2]; reset_all = cslrn[3];
  //   next_step = cslrn[4]

  // Notes on the sheet:
  //   r0
  //   r1
  //   r2
  //   r3
  //   r4
  //   r5
  //   r6
  //   fp
  //   pc
  //   sp
  //   ps
endmodule

// MEM BANK
module gpu_str_mem (
  input  [15:0] new_gen,
  input  [15:0] mask,
  input  [15:0] addr,
  input  reset_all,
  input  [15:0] pos,
  input  next_step,
  input  clock,
  input  life_on,
  output [15:0] str,
  output [15:0] pos_next
);

  wire comparator_1_eq, counter_1_q, counter_2_carry, multiplexer_3_out, not_1_out, or_1_out, or_2_out;
  wire [15:0] multiplexer_1_out, multiplexer_2_out, xor_1_out;

  // Probe on pos
  assign xor_1_out = str ^ mask;  // XOR_Gate xor_1, 16 bits wide
  Comparator #(.width(16), .mode("unsigned")) comparator_1 (.a(addr), .b(pos), .eq(comparator_1_eq));  // open: gt, lt
  Adder #(.width(16)) adder_1 (.a(pos), .b(16'h2), .out(pos_next));  // open: cin, cout
  Multiplexer #(.width(16), .enable("false")) multiplexer_1 (
    .in0(str), .in1(xor_1_out), .out(multiplexer_1_out), .sel(comparator_1_eq));
  or or_1 (or_1_out, counter_1_q, next_step);
  Counter #(.width(1), .max('h1)) counter_1 (.Q(counter_1_q), .clk(life_on));  // open: load, D, count, carry, clr
  Multiplexer #(.width(16)) multiplexer_2 (
    .in0(multiplexer_1_out), .in1(new_gen), .out(multiplexer_2_out), .sel(or_1_out), .en(not_1_out));
  Register #(.width(16)) register_1 (
    .D(multiplexer_2_out), .Q(str), .clk(multiplexer_3_out), .clr(reset_all));  // open: en
  not not_1 (not_1_out, multiplexer_3_out);
  Counter #(.width(1), .max('h1)) counter_2 (
    .count(comparator_1_eq), .carry(counter_2_carry), .clk(clock));  // open: load, D, Q, clr
  Multiplexer #(.enable("false")) multiplexer_3 (
    .in0(counter_2_carry), .in1(clock), .out(multiplexer_3_out), .sel(or_2_out));
  or or_2 (or_2_out, counter_1_q, next_step);
endmodule

// SCREEN CONTROL\nMODULE
module screen_control (
  input  [15:0] mask,
  input  [15:0] addr,
  input  [15:0] start_pos,
  input  [4:0] cslr,
  input  [31:0] str_up_in,
  input  [31:0] str_down_in,
  input  [15:0] str_right_in,
  input  [15:0] str_left_in,
  input  [3:0] corners_in,
  output [15:0] str0,
  output [15:0] str1,
  output [15:0] str2,
  output [15:0] str3,
  output [15:0] str4,
  output [15:0] str5,
  output [15:0] str6,
  output [15:0] str7,
  output [15:0] str8,
  output [15:0] str9,
  output [15:0] str10,
  output [15:0] str11,
  output [15:0] str12,
  output [15:0] str13,
  output [15:0] str14,
  output [15:0] str15,
  output [15:0] mask_2,
  output [4:0] cslr_2,
  output [15:0] str16,
  output [15:0] str17,
  output [15:0] str18,
  output [15:0] str19,
  output [15:0] str20,
  output [15:0] str21,
  output [15:0] str22,
  output [15:0] str23,
  output [15:0] str24,
  output [15:0] str25,
  output [15:0] str26,
  output [15:0] str27,
  output [15:0] str28,
  output [15:0] str29,
  output [15:0] str30,
  output [15:0] str31,
  output [15:0] next_pos,
  output [15:0] addr_pass,
  output [3:0] corners_out,
  output [31:0] str_down_out,
  output [31:0] str_up_out,
  output [15:0] str_right_out,
  output [15:0] str_left_out,
  output [15:0] next_gen_0,
  output [15:0] next_gen_1,
  output [15:0] next_gen_2,
  output [15:0] next_gen_3,
  output [15:0] next_gen_4,
  output [15:0] next_gen_5,
  output [15:0] next_gen_6,
  output [15:0] next_gen_7,
  output [15:0] next_gen_8,
  output [15:0] next_gen_9,
  output [15:0] next_gen_10,
  output [15:0] next_gen_11,
  output [15:0] next_gen_12,
  output [15:0] next_gen_13,
  output [15:0] next_gen_14,
  output [15:0] next_gen_15,
  output [15:0] next_gen_16,
  output [15:0] next_gen_17,
  output [15:0] next_gen_18,
  output [15:0] next_gen_19,
  output [15:0] next_gen_20,
  output [15:0] next_gen_21,
  output [15:0] next_gen_22,
  output [15:0] next_gen_23,
  output [15:0] next_gen_24,
  output [15:0] next_gen_25,
  output [15:0] next_gen_26,
  output [15:0] next_gen_27,
  output [15:0] next_gen_28,
  output [15:0] next_gen_29,
  output [15:0] next_gen_30,
  output [15:0] next_gen_31
);

  wire [15:0] gpu_str_mem_1_pos_next, gpu_str_mem_2_pos_next, gpu_str_mem_3_pos_next, gpu_str_mem_4_pos_next,
       gpu_str_mem_5_pos_next, gpu_str_mem_6_pos_next, gpu_str_mem_7_pos_next, gpu_str_mem_8_pos_next,
       gpu_str_mem_9_pos_next, gpu_str_mem_10_pos_next, gpu_str_mem_11_pos_next, gpu_str_mem_12_pos_next,
       gpu_str_mem_13_pos_next, gpu_str_mem_14_pos_next, gpu_str_mem_15_pos_next, gpu_str_mem_16_pos_next,
       gpu_str_mem_17_pos_next, gpu_str_mem_18_pos_next, gpu_str_mem_19_pos_next, gpu_str_mem_20_pos_next,
       gpu_str_mem_21_pos_next, gpu_str_mem_22_pos_next, gpu_str_mem_23_pos_next, gpu_str_mem_24_pos_next,
       gpu_str_mem_25_pos_next, gpu_str_mem_26_pos_next, gpu_str_mem_27_pos_next, gpu_str_mem_28_pos_next,
       gpu_str_mem_29_pos_next, gpu_str_mem_30_pos_next, start_pos_t;

  assign addr_pass = cslr[1] ? addr : 16'bz;  // Controlled_Buffer controlled_buffer_1
  gpu_str_mem gpu_str_mem_1 (
    .addr(addr_pass), .str({corners_out[0], str0[14:1], corners_out[1]}), .pos(start_pos), .clock(cslr[0]),
    .pos_next(gpu_str_mem_1_pos_next), .life_on(cslr[2]), .new_gen(next_gen_0), .mask(mask),
    .reset_all(cslr[3]), .next_step(cslr[4]));
  gpu_str_mem gpu_str_mem_2 (
    .addr(addr_pass), .str(str16), .pos(start_pos_t), .clock(cslr[0]), .pos_next(gpu_str_mem_2_pos_next),
    .life_on(cslr[2]), .new_gen(next_gen_16), .mask(mask), .reset_all(cslr[3]), .next_step(cslr[4]));
  gpu_str_mem gpu_str_mem_3 (
    .addr(addr_pass), .str(str1), .pos(gpu_str_mem_1_pos_next), .clock(cslr[0]),
    .pos_next(gpu_str_mem_3_pos_next), .life_on(cslr[2]), .new_gen(next_gen_1), .mask(mask),
    .reset_all(cslr[3]), .next_step(cslr[4]));
  gpu_str_mem gpu_str_mem_4 (
    .addr(addr_pass), .str(str17), .pos(gpu_str_mem_2_pos_next), .clock(cslr[0]),
    .pos_next(gpu_str_mem_4_pos_next), .life_on(cslr[2]), .new_gen(next_gen_17), .mask(mask),
    .reset_all(cslr[3]), .next_step(cslr[4]));
  gpu_str_mem gpu_str_mem_5 (
    .addr(addr_pass), .str(str2), .pos(gpu_str_mem_3_pos_next), .clock(cslr[0]),
    .pos_next(gpu_str_mem_5_pos_next), .life_on(cslr[2]), .new_gen(next_gen_2), .mask(mask),
    .reset_all(cslr[3]), .next_step(cslr[4]));
  gpu_str_mem gpu_str_mem_6 (
    .addr(addr_pass), .str(str18), .pos(gpu_str_mem_4_pos_next), .clock(cslr[0]),
    .pos_next(gpu_str_mem_6_pos_next), .life_on(cslr[2]), .new_gen(next_gen_18), .mask(mask),
    .reset_all(cslr[3]), .next_step(cslr[4]));
  gpu_compute_module gpu_compute_module_1 (
    .str0({corners_out[0], str0[14:1], corners_out[1]}), .str1(str1), .str2(str2), .str3(str3), .str4(str4),
    .str5(str5), .str6(str6), .str7(str7), .str8(str8), .str9(str9), .str10(str10), .str11(str11),
    .str12(str12), .str13(str13), .str14(str14), .str15(str15), .str16(str16), .str17(str17), .str18(str18),
    .str19(str19), .str20(str20), .str21(str21), .str22(str22), .str23(str23), .str24(str24), .str25(str25),
    .str26(str26), .str27(str27), .str28(str28), .str29(str29), .str30(str30),
    .str31({corners_out[3], str31[14:1], corners_out[2]}),
    .str_right({corners_in[3], str_right_in, corners_in[2]}),
    .str_left({corners_in[0], str_left_in, corners_in[1]}), .str_up(str_up_in), .str_down(str_down_in),
    .next_gen0(next_gen_0), .next_gen1(next_gen_1), .next_gen2(next_gen_2), .next_gen3(next_gen_3),
    .next_gen4(next_gen_4), .next_gen5(next_gen_5), .next_gen6(next_gen_6), .next_gen7(next_gen_7),
    .next_gen8(next_gen_8), .next_gen9(next_gen_9), .next_gen10(next_gen_10), .next_gen11(next_gen_11),
    .next_gen12(next_gen_12), .next_gen13(next_gen_13), .next_gen14(next_gen_14), .next_gen15(next_gen_15),
    .next_gen15_2(next_gen_16), .next_gen17(next_gen_17), .next_gen18(next_gen_18), .next_gen19(next_gen_19),
    .next_gen20(next_gen_20), .next_gen21(next_gen_21), .next_gen22(next_gen_22), .next_gen23(next_gen_23),
    .next_gen24(next_gen_24), .next_gen25(next_gen_25), .next_gen26(next_gen_26), .next_gen27(next_gen_27),
    .next_gen28(next_gen_28), .next_gen29(next_gen_29), .next_gen30(next_gen_30), .next_gen31(next_gen_31));
  gpu_str_mem gpu_str_mem_7 (
    .addr(addr_pass), .str(str3), .pos(gpu_str_mem_5_pos_next), .clock(cslr[0]),
    .pos_next(gpu_str_mem_7_pos_next), .life_on(cslr[2]), .new_gen(next_gen_3), .mask(mask),
    .reset_all(cslr[3]), .next_step(cslr[4]));
  gpu_str_mem gpu_str_mem_8 (
    .addr(addr_pass), .str(str19), .pos(gpu_str_mem_6_pos_next), .clock(cslr[0]),
    .pos_next(gpu_str_mem_8_pos_next), .life_on(cslr[2]), .new_gen(next_gen_19), .mask(mask),
    .reset_all(cslr[3]), .next_step(cslr[4]));
  gpu_str_mem gpu_str_mem_9 (
    .addr(addr_pass), .str(str4), .pos(gpu_str_mem_7_pos_next), .clock(cslr[0]),
    .pos_next(gpu_str_mem_9_pos_next), .life_on(cslr[2]), .new_gen(next_gen_4), .mask(mask),
    .reset_all(cslr[3]), .next_step(cslr[4]));
  gpu_str_mem gpu_str_mem_10 (
    .addr(addr_pass), .str(str20), .pos(gpu_str_mem_8_pos_next), .clock(cslr[0]),
    .pos_next(gpu_str_mem_10_pos_next), .life_on(cslr[2]), .new_gen(next_gen_20), .mask(mask),
    .reset_all(cslr[3]), .next_step(cslr[4]));
  gpu_str_mem gpu_str_mem_11 (
    .addr(addr_pass), .str(str5), .pos(gpu_str_mem_9_pos_next), .clock(cslr[0]),
    .pos_next(gpu_str_mem_11_pos_next), .life_on(cslr[2]), .new_gen(next_gen_5), .mask(mask),
    .reset_all(cslr[3]), .next_step(cslr[4]));
  gpu_str_mem gpu_str_mem_12 (
    .addr(addr_pass), .str(str21), .pos(gpu_str_mem_10_pos_next), .clock(cslr[0]),
    .pos_next(gpu_str_mem_12_pos_next), .life_on(cslr[2]), .new_gen(next_gen_21), .mask(mask),
    .reset_all(cslr[3]), .next_step(cslr[4]));
  gpu_str_mem gpu_str_mem_13 (
    .addr(addr_pass), .str(str6), .pos(gpu_str_mem_11_pos_next), .clock(cslr[0]),
    .pos_next(gpu_str_mem_13_pos_next), .life_on(cslr[2]), .new_gen(next_gen_6), .mask(mask),
    .reset_all(cslr[3]), .next_step(cslr[4]));
  gpu_str_mem gpu_str_mem_14 (
    .addr(addr_pass), .str(str22), .pos(gpu_str_mem_12_pos_next), .clock(cslr[0]),
    .pos_next(gpu_str_mem_14_pos_next), .life_on(cslr[2]), .new_gen(next_gen_22), .mask(mask),
    .reset_all(cslr[3]), .next_step(cslr[4]));
  gpu_str_mem gpu_str_mem_15 (
    .addr(addr_pass), .str(str7), .pos(gpu_str_mem_13_pos_next), .clock(cslr[0]),
    .pos_next(gpu_str_mem_15_pos_next), .life_on(cslr[2]), .new_gen(next_gen_7), .mask(mask),
    .reset_all(cslr[3]), .next_step(cslr[4]));
  gpu_str_mem gpu_str_mem_16 (
    .addr(addr_pass), .str(str23), .pos(gpu_str_mem_14_pos_next), .clock(cslr[0]),
    .pos_next(gpu_str_mem_16_pos_next), .life_on(cslr[2]), .new_gen(next_gen_23), .mask(mask),
    .reset_all(cslr[3]), .next_step(cslr[4]));
  gpu_str_mem gpu_str_mem_17 (
    .addr(addr_pass), .str(str8), .pos(gpu_str_mem_15_pos_next), .clock(cslr[0]),
    .pos_next(gpu_str_mem_17_pos_next), .life_on(cslr[2]), .new_gen(next_gen_8), .mask(mask),
    .reset_all(cslr[3]), .next_step(cslr[4]));
  gpu_str_mem gpu_str_mem_18 (
    .addr(addr_pass), .str(str24), .pos(gpu_str_mem_16_pos_next), .clock(cslr[0]),
    .pos_next(gpu_str_mem_18_pos_next), .life_on(cslr[2]), .new_gen(next_gen_24), .mask(mask),
    .reset_all(cslr[3]), .next_step(cslr[4]));
  gpu_str_mem gpu_str_mem_19 (
    .addr(addr_pass), .str(str9), .pos(gpu_str_mem_17_pos_next), .clock(cslr[0]),
    .pos_next(gpu_str_mem_19_pos_next), .life_on(cslr[2]), .new_gen(next_gen_9), .mask(mask),
    .reset_all(cslr[3]), .next_step(cslr[4]));
  gpu_str_mem gpu_str_mem_20 (
    .addr(addr_pass), .str(str25), .pos(gpu_str_mem_18_pos_next), .clock(cslr[0]),
    .pos_next(gpu_str_mem_20_pos_next), .life_on(cslr[2]), .new_gen(next_gen_25), .mask(mask),
    .reset_all(cslr[3]), .next_step(cslr[4]));
  gpu_str_mem gpu_str_mem_21 (
    .addr(addr_pass), .str(str10), .pos(gpu_str_mem_19_pos_next), .clock(cslr[0]),
    .pos_next(gpu_str_mem_21_pos_next), .life_on(cslr[2]), .new_gen(next_gen_10), .mask(mask),
    .reset_all(cslr[3]), .next_step(cslr[4]));
  gpu_str_mem gpu_str_mem_22 (
    .addr(addr_pass), .str(str26), .pos(gpu_str_mem_20_pos_next), .clock(cslr[0]),
    .pos_next(gpu_str_mem_22_pos_next), .life_on(cslr[2]), .new_gen(next_gen_26), .mask(mask),
    .reset_all(cslr[3]), .next_step(cslr[4]));
  gpu_str_mem gpu_str_mem_23 (
    .addr(addr_pass), .str(str11), .pos(gpu_str_mem_21_pos_next), .clock(cslr[0]),
    .pos_next(gpu_str_mem_23_pos_next), .life_on(cslr[2]), .new_gen(next_gen_11), .mask(mask),
    .reset_all(cslr[3]), .next_step(cslr[4]));
  gpu_str_mem gpu_str_mem_24 (
    .addr(addr_pass), .str(str27), .pos(gpu_str_mem_22_pos_next), .clock(cslr[0]),
    .pos_next(gpu_str_mem_24_pos_next), .life_on(cslr[2]), .new_gen(next_gen_27), .mask(mask),
    .reset_all(cslr[3]), .next_step(cslr[4]));
  gpu_str_mem gpu_str_mem_25 (
    .addr(addr_pass), .str(str12), .pos(gpu_str_mem_23_pos_next), .clock(cslr[0]),
    .pos_next(gpu_str_mem_25_pos_next), .life_on(cslr[2]), .new_gen(next_gen_12), .mask(mask),
    .reset_all(cslr[3]), .next_step(cslr[4]));
  gpu_str_mem gpu_str_mem_26 (
    .addr(addr_pass), .str(str28), .pos(gpu_str_mem_24_pos_next), .clock(cslr[0]),
    .pos_next(gpu_str_mem_26_pos_next), .life_on(cslr[2]), .new_gen(next_gen_28), .mask(mask),
    .reset_all(cslr[3]), .next_step(cslr[4]));
  gpu_str_mem gpu_str_mem_27 (
    .addr(addr_pass), .str(str13), .pos(gpu_str_mem_25_pos_next), .clock(cslr[0]),
    .pos_next(gpu_str_mem_27_pos_next), .life_on(cslr[2]), .new_gen(next_gen_13), .mask(mask),
    .reset_all(cslr[3]), .next_step(cslr[4]));
  gpu_str_mem gpu_str_mem_28 (
    .addr(addr_pass), .str(str29), .pos(gpu_str_mem_26_pos_next), .clock(cslr[0]),
    .pos_next(gpu_str_mem_28_pos_next), .life_on(cslr[2]), .new_gen(next_gen_29), .mask(mask),
    .reset_all(cslr[3]), .next_step(cslr[4]));
  gpu_str_mem gpu_str_mem_29 (
    .addr(addr_pass), .str(str14), .pos(gpu_str_mem_27_pos_next), .clock(cslr[0]),
    .pos_next(gpu_str_mem_29_pos_next), .life_on(cslr[2]), .new_gen(next_gen_14), .mask(mask),
    .reset_all(cslr[3]), .next_step(cslr[4]));
  gpu_str_mem gpu_str_mem_30 (
    .addr(addr_pass), .str(str30), .pos(gpu_str_mem_28_pos_next), .clock(cslr[0]),
    .pos_next(gpu_str_mem_30_pos_next), .life_on(cslr[2]), .new_gen(next_gen_30), .mask(mask),
    .reset_all(cslr[3]), .next_step(cslr[4]));
  gpu_str_mem gpu_str_mem_31 (
    .addr(addr_pass), .str(str15), .pos(gpu_str_mem_29_pos_next), .clock(cslr[0]), .pos_next(start_pos_t),
    .life_on(cslr[2]), .new_gen(next_gen_15), .mask(mask), .reset_all(cslr[3]), .next_step(cslr[4]));
  gpu_str_mem gpu_str_mem_32 (
    .addr(addr_pass), .str({corners_out[3], str31[14:1], corners_out[2]}), .pos(gpu_str_mem_30_pos_next),
    .clock(cslr[0]), .pos_next(next_pos), .life_on(cslr[2]), .new_gen(next_gen_31), .mask(mask),
    .reset_all(cslr[3]), .next_step(cslr[4]));

  assign cslr_2 = cslr;
  assign mask_2 = mask;
  assign {str0[15], str0[0]} = {corners_out[0], corners_out[1]};
  assign {str31[15], str31[0]} = corners_out[3:2];
  assign str_down_out = {corners_out[2], str30[0], str29[0], str28[0], str27[0], str26[0], str25[0], str24[0], str23[0], str22[0], str21[0], str20[0], str19[0], str18[0], str17[0], str16[0], str15[0], str14[0], str13[0], str12[0], str11[0], str10[0], str9[0], str8[0], str7[0], str6[0], str5[0], str4[0], str3[0], str2[0], str1[0], corners_out[1]};
  assign str_left_out = {corners_out[0], str0[14:1], corners_out[1]};
  assign str_right_out = {corners_out[3], str31[14:1], corners_out[2]};
  assign str_up_out = {corners_out[3], str30[15], str29[15], str28[15], str27[15], str26[15], str25[15], str24[15], str23[15], str22[15], str21[15], str20[15], str19[15], str18[15], str17[15], str16[15], str15[15], str14[15], str13[15], str12[15], str11[15], str10[15], str9[15], str8[15], str7[15], str6[15], str5[15], str4[15], str3[15], str2[15], str1[15], corners_out[0]};

  // Other names for the same wires on the sheet: addr_t[15:0] = addr_pass; up0 = corners_out[0];
  //   down0 = corners_out[1]; clock = cslr[0]; set = cslr[1]; life_on = cslr[2]; reset = cslr[3]; next_step = cslr[4];
  //   ng0[15:0] = next_gen_0; ng1[15:0] = next_gen_1; ng2[15:0] = next_gen_2; ng3[15:0] = next_gen_3;
  //   ng4[15:0] = next_gen_4; ng5[15:0] = next_gen_5; ng6[15:0] = next_gen_6; ng7[15:0] = next_gen_7;
  //   ng8[15:0] = next_gen_8; ng9[15:0] = next_gen_9; ng10[15:0] = next_gen_10; ng11[15:0] = next_gen_11;
  //   ng12[15:0] = next_gen_12; ng13[15:0] = next_gen_13; ng14[15:0] = next_gen_14; ng15[15:0] = next_gen_15;
  //   ng16[15:0] = next_gen_16; ng17[15:0] = next_gen_17; ng18[15:0] = next_gen_18; ng19[15:0] = next_gen_19;
  //   ng20[15:0] = next_gen_20; ng21[15:0] = next_gen_21; ng22[15:0] = next_gen_22; ng23[15:0] = next_gen_23;
  //   ng24[15:0] = next_gen_24; ng25[15:0] = next_gen_25; ng26[15:0] = next_gen_26; ng27[15:0] = next_gen_27;
  //   ng28[15:0] = next_gen_28; ng29[15:0] = next_gen_29; ng30[15:0] = next_gen_30; ng31[15:0] = next_gen_31;
  //   down7 = str7[0]; down8 = str8[0]; down9 = str9[0]; up9 = str9[15]; down10 = str10[0]; up10 = str10[15];
  //   down11 = str11[0]; up11 = str11[15]; down12 = str12[0]; up12 = str12[15]; down13 = str13[0]; up13 = str13[15];
  //   down14 = str14[0]; up14 = str14[15]; down15 = str15[0]; up15 = str15[15]; down23 = str23[0]; down24 = str24[0];
  //   down25 = str25[0]; up25 = str25[15]; down26 = str26[0]; up26 = str26[15]; down27 = str27[0]; up27 = str27[15];
  //   down28 = str28[0]; up28 = str28[15]; down29 = str29[0]; up29 = str29[15]; down30 = str30[0]; up30 = str30[15];
  //   down1 = str1[0]; down2 = str2[0]; down3 = str3[0]; down4 = str4[0]; down5 = str5[0]; down6 = str6[0];
  //   down16 = str16[0]; down17 = str17[0]; down18 = str18[0]; down19 = str19[0]; down20 = str20[0];
  //   down21 = str21[0]; down22 = str22[0]; down31 = corners_out[2]; up31 = corners_out[3]; up1 = str1[15];
  //   up2 = str2[15]; up3 = str3[15]; up4 = str4[15]; up5 = str5[15]; up6 = str6[15]; up7 = str7[15]; up8 = str8[15];
  //   up16 = str16[15]; up17 = str17[15]; up18 = str18[15]; up19 = str19[15]; up20 = str20[15]; up21 = str21[15];
  //   up22 = str22[15]; up23 = str23[15]; up24 = str24[15]

  // Notes on the sheet:
  //   *ВСТАВЬТЕ ВИДЕОКАРТУ ИЛИ УДАЛИТЕ*
endmodule

// button controller
module but_control (
  input  clock,
  input  life_on,
  input  IAck,
  input  read,
  input  [15:0] addr,
  input  up,
  input  down,
  input  rst,
  input  right,
  input  left,
  input  plane,
  input  bashni,
  output IRQ,
  output [15:0] data,
  output [5:0] vec
);

  wire bashni_t, comparator_1_eq, counter_1_carry, counter_2_carry, counter_3_carry, counter_5_carry,
       counter_6_carry, counter_8_carry, counter_9_carry, down_t, got, life_flag, not_1_out, not_2_out,
       not_3_out, not_4_out, not_5_out, not_6_out, not_7_out;
  wire [6:1] flag;
  wire [15:0] counter_7_q;

  Counter #(.width(4), .max('hf)) counter_1 (
    .count(flag[1]), .carry(counter_1_carry), .clk(clock), .clr(not_1_out));  // open: load, D, Q
  not not_1 (not_1_out, flag[1]);
  Counter #(.width(4), .max('hf)) counter_2 (
    .count(flag[2]), .carry(counter_2_carry), .clk(clock), .clr(not_2_out));  // open: load, D, Q
  not not_2 (not_2_out, flag[2]);
  Counter #(.width(4), .max('hf)) counter_3 (
    .count(bashni_t), .carry(counter_3_carry), .clk(clock), .clr(not_3_out));  // open: load, D, Q
  not not_3 (not_3_out, bashni_t);
  D_Flip_Flop d_ff_1 (.clk(up), .D(1'b1), .Q(flag[1]), .reset(counter_1_carry));  // open: Qn, preset, en
  D_Flip_Flop d_ff_2 (.clk(right), .D(1'b1), .Q(flag[2]), .reset(counter_2_carry));  // open: Qn, preset, en
  D_Flip_Flop d_ff_3 (.clk(bashni), .D(1'b1), .Q(bashni_t), .reset(counter_3_carry));  // open: Qn, preset, en
  Counter #(.width(1), .max('h1)) counter_4 (.Q(life_flag), .clk(life_on));  // open: load, D, count, carry, clr
  Counter #(.width(4), .max('hf)) counter_5 (
    .count(down_t), .carry(counter_5_carry), .clk(clock), .clr(not_4_out));  // open: load, D, Q
  not not_4 (not_4_out, down_t);
  Counter #(.width(4), .max('hf)) counter_6 (
    .count(flag[3]), .carry(counter_6_carry), .clk(clock), .clr(not_5_out));  // open: load, D, Q
  not not_5 (not_5_out, flag[3]);
  D_Flip_Flop d_ff_4 (.clk(down), .D(1'b1), .Q(down_t), .reset(counter_5_carry));  // open: Qn, preset, en
  D_Flip_Flop d_ff_5 (.clk(left), .D(1'b1), .Q(flag[3]), .reset(counter_6_carry));  // open: Qn, preset, en
  assign vec = flag[1] ? 6'b000101 : 6'bz;  // Controlled_Buffer controlled_buffer_1
  assign vec = flag[2] ? 6'b000110 : 6'bz;  // Controlled_Buffer controlled_buffer_2
  assign vec = down_t ? 6'b000111 : 6'bz;  // Controlled_Buffer controlled_buffer_3
  assign vec = flag[3] ? 6'b001000 : 6'bz;  // Controlled_Buffer controlled_buffer_4
  assign vec = life_on ? 6'b001001 : 6'bz;  // Controlled_Buffer controlled_buffer_5
  assign vec = flag[5] ? 6'b001010 : 6'bz;  // Controlled_Buffer controlled_buffer_6
  assign vec = flag[6] ? 6'b001011 : 6'bz;  // Controlled_Buffer controlled_buffer_7
  assign vec = bashni_t ? 6'b001100 : 6'bz;  // Controlled_Buffer controlled_buffer_8
  Counter #(.width(16), .max('h1)) counter_7 (.Q(counter_7_q), .clk(IRQ));  // open: load, D, count, carry, clr
  assign data = got ? counter_7_q : 16'bz;  // Controlled_Buffer controlled_buffer_9
  and and_1 (got, read, comparator_1_eq);
  Comparator #(.width(16)) comparator_1 (.a(addr), .b(16'hfff0), .eq(comparator_1_eq));  // open: gt, lt
  or or_1 (IRQ, life_on, flag[1], flag[2], flag[3], down_t, flag[5], flag[6], bashni_t, 1'b0, 1'b0, 1'b0, 1'b0, 1'b0, 1'b0, 1'b0, 1'b0);
  D_Flip_Flop d_ff_6 (.clk(rst), .D(1'b1), .Q(flag[5]), .reset(counter_8_carry));  // open: Qn, preset, en
  Counter #(.width(4), .max('hf)) counter_8 (
    .count(flag[5]), .carry(counter_8_carry), .clk(clock), .clr(not_6_out));  // open: load, D, Q
  not not_6 (not_6_out, flag[5]);
  D_Flip_Flop d_ff_7 (.clk(plane), .D(1'b1), .Q(flag[6]), .reset(counter_9_carry));  // open: Qn, preset, en
  Counter #(.width(4), .max('hf)) counter_9 (
    .count(flag[6]), .carry(counter_9_carry), .clk(clock), .clr(not_7_out));  // open: load, D, Q
  not not_7 (not_7_out, flag[6]);

  // Other names for the same wires on the sheet: flag (some bits) = {bashni_t, down_t, life_on}; up_t = flag[1];
  //   right_t = flag[2]; left_t = flag[3]; rst_t = flag[5]; plane_t = flag[6]

  // Notes on the sheet:
  //   data: pull=down
  //   addr: pull=down
endmodule
