// Logisim project main_old.circ as structural Verilog: 7 circuits, main circuit main
module main (
  input  Hold
);

  wire \bit , cdm16e_1_p2, cdm16e_1_p5, cdm16e_1_p6, cdm16e_1_p7, cdm16e_1_p8, cdm16e_1_p9, cdm16e_1_p10,
       cdm16e_1_p11, cdm16e_1_p12, cdm16e_1_p13, cl, mem, not_1_out, r_w, screen_control_1_p37,
       screen_control_2_clock_out, screen_control_3_clock_out, screen_control_4_clock_out;
  wire [15:0] addr, cdm16e_1_p18, cdm16e_1_p19, data, debugger_1_p1, debugger_1_p2, debugger_1_p3,
       debugger_1_p4, debugger_1_p5, debugger_1_p6, debugger_1_p7, debugger_1_p8, debugger_1_p9, np1, np2,
       np3, r1, screen_control_1_p1, screen_control_1_p6, screen_control_1_p7, screen_control_1_p8,
       screen_control_1_p9, screen_control_1_p10, screen_control_1_p11, screen_control_1_p12,
       screen_control_1_p13, screen_control_1_p14, screen_control_1_p15, screen_control_1_p16,
       screen_control_1_p17, screen_control_1_p18, screen_control_1_p19, screen_control_1_p20,
       screen_control_1_p21, screen_control_1_p22, screen_control_1_p23, screen_control_1_p24,
       screen_control_1_p25, screen_control_1_p26, screen_control_1_p27, screen_control_1_p28,
       screen_control_1_p29, screen_control_1_p30, screen_control_1_p31, screen_control_1_p32,
       screen_control_1_p33, screen_control_1_p34, screen_control_1_p35, screen_control_1_p36,
       screen_control_1_p38, screen_control_1_p39, screen_control_1_p40, screen_control_1_p41,
       screen_control_1_p42, screen_control_1_p43, screen_control_2_addr_pass, screen_control_2_data_pass,
       screen_control_2_next_pos, screen_control_3_addr_pass, screen_control_3_data_pass,
       screen_control_3_next_pos, screen_control_4_addr_pass, screen_control_4_data_pass,
       screen_control_4_next_pos, screen_control_5__14, screen_control_5__14_2, screen_control_5_str0_2,
       screen_control_5_str1_2, screen_control_5_str2_2, screen_control_5_str3_2, screen_control_5_str4_2,
       screen_control_5_str5_2, screen_control_5_str6_2, screen_control_5_str7_2, screen_control_5_str8_2,
       screen_control_5_str9_2, screen_control_5_str10_2, screen_control_5_str11_2, screen_control_5_str12,
       screen_control_5_str12_2, screen_control_5_str13, screen_control_5_str13_2, screen_control_5_str15,
       screen_control_5_str15_2;

  // Probe on cdm16e_1_p2
  // Probe on cdm16e_1_p2
  // Probe on cdm16e_1_p2
  Clock clock_1 (.out(cl));
  // Probe on r1
  // Probe on r1
  // Probe on r1
  // Probe on cdm16e_1_p5
  // Probe on cdm16e_1_p5
  // Probe on cdm16e_1_p5
  // cdm16e cdm16e_1: pin names not known; wires that end beside it: Hold, cdm16e_1_p2, r1, cl, cdm16e_1_p5, cdm16e_1_p6, cdm16e_1_p7, cdm16e_1_p8, cdm16e_1_p9, cdm16e_1_p10, cdm16e_1_p11, cdm16e_1_p12, cdm16e_1_p13, mem, r_w, \bit , addr, cdm16e_1_p18, cdm16e_1_p19
  // Probe on data
  // Probe on data
  // Probe on data
  // Probe on data
  // Probe on addr
  // Probe on addr
  // Probe on addr
  // Probe on addr
  // Probe on cdm16e_1_p6
  // Probe on cdm16e_1_p6
  // Probe on cdm16e_1_p6
  assign data = not_1_out ? cdm16e_1_p18 : 16'bz;  // Controlled_Buffer controlled_buffer_1
  not not_1 (not_1_out, r_w);
  assign cdm16e_1_p19 = r_w ? data : 16'bz;  // Controlled_Buffer controlled_buffer_2
  // Probe on cdm16e_1_p7
  // Probe on cdm16e_1_p7
  // Probe on cdm16e_1_p7
  // Probe on cdm16e_1_p8
  // Probe on cdm16e_1_p8
  // Probe on cdm16e_1_p8
  DotMatrix #(.matrixcols(32), .matrixrows(16)) dotmatrix_1 (
    .col0(screen_control_1_p1), .col1(screen_control_1_p6), .col2(screen_control_1_p7),
    .col3(screen_control_1_p8), .col4(screen_control_1_p9), .col5(screen_control_1_p10),
    .col6(screen_control_1_p11), .col7(screen_control_1_p12), .col8(screen_control_1_p13),
    .col9(screen_control_1_p14), .col10(screen_control_1_p15), .col11(screen_control_1_p16),
    .col12(screen_control_1_p17), .col13(screen_control_1_p18), .col14(screen_control_1_p19),
    .col15(screen_control_1_p20), .col16(screen_control_1_p21), .col17(screen_control_1_p22),
    .col18(screen_control_1_p23), .col19(screen_control_1_p24), .col20(screen_control_1_p25),
    .col21(screen_control_1_p26), .col22(screen_control_1_p27), .col23(screen_control_1_p28),
    .col24(screen_control_1_p29), .col25(screen_control_1_p30), .col26(screen_control_1_p31),
    .col27(screen_control_1_p32), .col28(screen_control_1_p33), .col29(screen_control_1_p34),
    .col30(screen_control_1_p35), .col31(screen_control_1_p36));
  // Probe on cdm16e_1_p9
  // Probe on cdm16e_1_p9
  // Probe on cdm16e_1_p9
  // Probe on cdm16e_1_p10
  // Probe on cdm16e_1_p10
  // Probe on cdm16e_1_p10
  // RAM ram_1: pin names not known; wires that end beside it: addr, \bit , mem, cl, r_w, data
  // screen_control screen_control_1: pin names not known; wires that end beside it: screen_control_1_p1, cl, data, addr, r1, screen_control_1_p6, screen_control_1_p7, screen_control_1_p8, screen_control_1_p9, screen_control_1_p10, screen_control_1_p11, screen_control_1_p12, screen_control_1_p13, screen_control_1_p14, screen_control_1_p15, screen_control_1_p16, screen_control_1_p17, screen_control_1_p18, screen_control_1_p19, screen_control_1_p20, screen_control_1_p21, screen_control_1_p22, screen_control_1_p23, screen_control_1_p24, screen_control_1_p25, screen_control_1_p26, screen_control_1_p27, screen_control_1_p28, screen_control_1_p29, screen_control_1_p30, screen_control_1_p31, screen_control_1_p32, screen_control_1_p33, screen_control_1_p34, screen_control_1_p35, screen_control_1_p36, screen_control_1_p37, screen_control_1_p38, screen_control_1_p39, screen_control_1_p40, screen_control_1_p41, screen_control_1_p42, screen_control_1_p43
  screen_control screen_control_2 (
    .clock(cl), .data(data), .addr(addr), .start_pos(np1), .next_pos(screen_control_2_next_pos),
    .clock_out(screen_control_2_clock_out), .data_pass(screen_control_2_data_pass),
    .addr_pass(screen_control_2_addr_pass));  // open: str0, str1, str2, str3, str4, str5, str6, str7, str8, str9, str10, str11, str12, str13, _14, str15, str0_2, str1_2, str2_2, str3_2, str4_2, str5_2, str6_2, str7_2, str8_2, str9_2, str10_2, str11_2, str12_2, str13_2, _14_2, str15_2, str_up_out, str_down_out, str_up_in, str_down_in, str_right_out, str_left_out, str_right_in, str_left_in, corners_in, corners_out
  screen_control screen_control_3 (
    .clock(cl), .data(data), .addr(addr), .start_pos(np2), .next_pos(screen_control_3_next_pos),
    .clock_out(screen_control_3_clock_out), .data_pass(screen_control_3_data_pass),
    .addr_pass(screen_control_3_addr_pass));  // open: str0, str1, str2, str3, str4, str5, str6, str7, str8, str9, str10, str11, str12, str13, _14, str15, str0_2, str1_2, str2_2, str3_2, str4_2, str5_2, str6_2, str7_2, str8_2, str9_2, str10_2, str11_2, str12_2, str13_2, _14_2, str15_2, str_up_out, str_down_out, str_up_in, str_down_in, str_right_out, str_left_out, str_right_in, str_left_in, corners_in, corners_out
  screen_control screen_control_4 (
    .clock(cl), .data(data), .addr(addr), .start_pos(np3), .next_pos(screen_control_4_next_pos),
    .clock_out(screen_control_4_clock_out), .data_pass(screen_control_4_data_pass),
    .addr_pass(screen_control_4_addr_pass));  // open: str0, str1, str2, str3, str4, str5, str6, str7, str8, str9, str10, str11, str12, str13, _14, str15, str0_2, str1_2, str2_2, str3_2, str4_2, str5_2, str6_2, str7_2, str8_2, str9_2, str10_2, str11_2, str12_2, str13_2, _14_2, str15_2, str_up_out, str_down_out, str_up_in, str_down_in, str_right_out, str_left_out, str_right_in, str_left_in, corners_in, corners_out
  // Probe on cdm16e_1_p11
  // Probe on cdm16e_1_p11
  // Probe on cdm16e_1_p11
  // Debugger debugger_1: pin names not known; wires that end beside it: debugger_1_p1, debugger_1_p2, debugger_1_p3, debugger_1_p4, debugger_1_p5, debugger_1_p6, debugger_1_p7, debugger_1_p8, debugger_1_p9
  // Probe on cdm16e_1_p12
  // Probe on cdm16e_1_p12
  // Probe on cdm16e_1_p12
  // Probe on cdm16e_1_p13
  // Probe on cdm16e_1_p13
  // Probe on cdm16e_1_p13
  screen_control screen_control_5 (
    .clock(screen_control_1_p37), .data(screen_control_1_p38), .addr(screen_control_1_p39),
    .start_pos(screen_control_1_p40), .str0(screen_control_1_p41), .str1(screen_control_1_p42),
    .str2(screen_control_1_p43), .str3(debugger_1_p1), .str4(debugger_1_p2), .str5(debugger_1_p3),
    .str6(debugger_1_p4), .str7(debugger_1_p5), .str8(debugger_1_p6), .str9(debugger_1_p7),
    .str10(debugger_1_p8), .str11(debugger_1_p9), .str12(screen_control_5_str12),
    .str13(screen_control_5_str13), ._14(screen_control_5__14), .str15(screen_control_5_str15),
    .str0_2(screen_control_5_str0_2), .str1_2(screen_control_5_str1_2), .str2_2(screen_control_5_str2_2),
    .str3_2(screen_control_5_str3_2), .str4_2(screen_control_5_str4_2), .str5_2(screen_control_5_str5_2),
    .str6_2(screen_control_5_str6_2), .str7_2(screen_control_5_str7_2), .str8_2(screen_control_5_str8_2),
    .str9_2(screen_control_5_str9_2), .str10_2(screen_control_5_str10_2), .str11_2(screen_control_5_str11_2),
    .str12_2(screen_control_5_str12_2), .str13_2(screen_control_5_str13_2), ._14_2(screen_control_5__14_2),
    .str15_2(screen_control_5_str15_2), .next_pos(np1));  // open: clock_out, data_pass, addr_pass, str_up_out, str_down_out, str_up_in, str_down_in, str_right_out, str_left_out, str_right_in, str_left_in, corners_in, corners_out
  screen_control screen_control_6 (
    .clock(screen_control_2_clock_out), .data(screen_control_2_data_pass), .addr(screen_control_2_addr_pass),
    .start_pos(screen_control_2_next_pos), .next_pos(np2));  // open: str0, str1, str2, str3, str4, str5, str6, str7, str8, str9, str10, str11, str12, str13, _14, str15, str0_2, str1_2, str2_2, str3_2, str4_2, str5_2, str6_2, str7_2, str8_2, str9_2, str10_2, str11_2, str12_2, str13_2, _14_2, str15_2, clock_out, data_pass, addr_pass, str_up_out, str_down_out, str_up_in, str_down_in, str_right_out, str_left_out, str_right_in, str_left_in, corners_in, corners_out
  screen_control screen_control_7 (
    .clock(screen_control_3_clock_out), .data(screen_control_3_data_pass), .addr(screen_control_3_addr_pass),
    .start_pos(screen_control_3_next_pos), .next_pos(np3));  // open: str0, str1, str2, str3, str4, str5, str6, str7, str8, str9, str10, str11, str12, str13, _14, str15, str0_2, str1_2, str2_2, str3_2, str4_2, str5_2, str6_2, str7_2, str8_2, str9_2, str10_2, str11_2, str12_2, str13_2, _14_2, str15_2, clock_out, data_pass, addr_pass, str_up_out, str_down_out, str_up_in, str_down_in, str_right_out, str_left_out, str_right_in, str_left_in, corners_in, corners_out
  screen_control screen_control_8 (
    .clock(screen_control_4_clock_out), .data(screen_control_4_data_pass), .addr(screen_control_4_addr_pass),
    .start_pos(screen_control_4_next_pos));  // open: str0, str1, str2, str3, str4, str5, str6, str7, str8, str9, str10, str11, str12, str13, _14, str15, str0_2, str1_2, str2_2, str3_2, str4_2, str5_2, str6_2, str7_2, str8_2, str9_2, str10_2, str11_2, str12_2, str13_2, _14_2, str15_2, next_pos, clock_out, data_pass, addr_pass, str_up_out, str_down_out, str_up_in, str_down_in, str_right_out, str_left_out, str_right_in, str_left_in, corners_in, corners_out
endmodule

module data_sel (
  input  [15:0] out,
  input  r_w,
  input  [15:0] in,
  output [15:0] data
);

  wire not_1_out;

  assign data = not_1_out ? out : 16'bz;  // Controlled_Buffer controlled_buffer_1
  not not_1 (not_1_out, r_w);
  assign in = r_w ? data : 16'bz;  // Controlled_Buffer controlled_buffer_2
endmodule

// MEM BANK
module gpu_str_mem (
  input  [15:0] data,
  input  [15:0] addr,
  input  clock,
  input  [15:0] pos,
  output [15:0] str,
  output [15:0] pos_next
);

  wire comparator_1_eq;
  wire [15:0] multiplexer_1_out;

  Comparator #(.width(16), .mode("unsigned")) comparator_1 (.a(addr), .b(pos), .eq(comparator_1_eq));  // open: gt, lt
  Adder #(.width(16)) adder_1 (.a(pos), .b(16'h2), .out(pos_next));  // open: cin, cout
  Multiplexer #(.width(16)) multiplexer_1 (
    .in0(str), .in1(data), .out(multiplexer_1_out), .sel(comparator_1_eq));  // open: en
  Register #(.width(16)) register_1 (.D(multiplexer_1_out), .Q(str), .clk(clock));  // open: en, clr
endmodule

// SCREEN CONTROL\nMODULE
module screen_control (
  input  [15:0] data,
  input  [15:0] addr,
  input  clock,
  input  [15:0] start_pos,
  input  [31:0] str_up_in,
  input  [31:0] str_down_in,
  input  [15:0] str_right_in,
  input  [15:0] str_left_in,
  input  [3:0] corners_in,
  output [15:0] str0,
  output [15:0] str1,
  output [15:0] str2,
  output [15:0] str3,
  output [15:0] str4,
  output [15:0] str5,
  output [15:0] str6,
  output [15:0] str7,
  output [15:0] str8,
  output [15:0] str9,
  output [15:0] str10,
  output [15:0] str11,
  output [15:0] str12,
  output [15:0] str13,
  output [15:0] _14,
  output [15:0] str15,
  output [15:0] str0_2,
  output [15:0] str1_2,
  output [15:0] str2_2,
  output [15:0] str3_2,
  output [15:0] str4_2,
  output [15:0] str5_2,
  output [15:0] str6_2,
  output [15:0] str7_2,
  output [15:0] str8_2,
  output [15:0] str9_2,
  output [15:0] str10_2,
  output [15:0] str11_2,
  output [15:0] str12_2,
  output [15:0] str13_2,
  output [15:0] _14_2,
  output [15:0] str15_2,
  output [15:0] data_pass,
  output clock_out,
  output [15:0] addr_pass,
  output [15:0] next_pos,
  output [31:0] str_down_out,
  output [31:0] str_up_out,
  output [15:0] str_right_out,
  output [3:0] corners_out,
  output [15:0] str_left_out
);

  wire [15:0] gpu_str_mem_1_pos_next, gpu_str_mem_2_pos_next, gpu_str_mem_3_pos_next, gpu_str_mem_4_pos_next,
       gpu_str_mem_5_pos_next, gpu_str_mem_6_pos_next, gpu_str_mem_7_pos_next, gpu_str_mem_8_pos_next,
       gpu_str_mem_9_pos_next, gpu_str_mem_10_pos_next, gpu_str_mem_11_pos_next, gpu_str_mem_12_pos_next,
       gpu_str_mem_13_pos_next, gpu_str_mem_14_pos_next, gpu_str_mem_15_pos_next, gpu_str_mem_16_pos_next,
       gpu_str_mem_17_pos_next, gpu_str_mem_18_pos_next, gpu_str_mem_19_pos_next, gpu_str_mem_20_pos_next,
       gpu_str_mem_21_pos_next, gpu_str_mem_22_pos_next, gpu_str_mem_23_pos_next, gpu_str_mem_24_pos_next,
       gpu_str_mem_25_pos_next, gpu_str_mem_26_pos_next, gpu_str_mem_27_pos_next, gpu_str_mem_28_pos_next,
       gpu_str_mem_29_pos_next, gpu_str_mem_30_pos_next, gpu_str_mem_31_pos_next;

  gpu_str_mem gpu_str_mem_1 (
    .data(data), .addr(addr), .str({corners_out[1], str0[14:1], corners_out[0]}), .pos(start_pos),
    .clock(clock), .pos_next(gpu_str_mem_1_pos_next));
  gpu_str_mem gpu_str_mem_2 (
    .data(data), .addr(addr), .str(str2), .pos(gpu_str_mem_3_pos_next), .clock(clock),
    .pos_next(gpu_str_mem_2_pos_next));
  gpu_str_mem gpu_str_mem_3 (
    .data(data), .addr(addr), .str(str1), .pos(gpu_str_mem_1_pos_next), .clock(clock),
    .pos_next(gpu_str_mem_3_pos_next));
  gpu_str_mem gpu_str_mem_4 (
    .data(data), .addr(addr), .str(str3), .pos(gpu_str_mem_2_pos_next), .clock(clock),
    .pos_next(gpu_str_mem_4_pos_next));
  gpu_str_mem gpu_str_mem_5 (
    .data(data), .addr(addr), .str(str5), .pos(gpu_str_mem_6_pos_next), .clock(clock),
    .pos_next(gpu_str_mem_5_pos_next));
  gpu_str_mem gpu_str_mem_6 (
    .data(data), .addr(addr), .str(str4), .pos(gpu_str_mem_4_pos_next), .clock(clock),
    .pos_next(gpu_str_mem_6_pos_next));
  gpu_str_mem gpu_str_mem_7 (
    .data(data), .addr(addr), .str(str7), .pos(gpu_str_mem_8_pos_next), .clock(clock),
    .pos_next(gpu_str_mem_7_pos_next));
  gpu_str_mem gpu_str_mem_8 (
    .data(data), .addr(addr), .str(str6), .pos(gpu_str_mem_5_pos_next), .clock(clock),
    .pos_next(gpu_str_mem_8_pos_next));
  gpu_str_mem gpu_str_mem_9 (
    .data(data), .addr(addr), .str(str8), .pos(gpu_str_mem_7_pos_next), .clock(clock),
    .pos_next(gpu_str_mem_9_pos_next));
  gpu_str_mem gpu_str_mem_10 (
    .data(data), .addr(addr), .str(str10), .pos(gpu_str_mem_11_pos_next), .clock(clock),
    .pos_next(gpu_str_mem_10_pos_next));
  gpu_str_mem gpu_str_mem_11 (
    .data(data), .addr(addr), .str(str9), .pos(gpu_str_mem_9_pos_next), .clock(clock),
    .pos_next(gpu_str_mem_11_pos_next));
  gpu_str_mem gpu_str_mem_12 (
    .data(data), .addr(addr), .str(str11), .pos(gpu_str_mem_10_pos_next), .clock(clock),
    .pos_next(gpu_str_mem_12_pos_next));
  gpu_str_mem gpu_str_mem_13 (
    .data(data), .addr(addr), .str(str12), .pos(gpu_str_mem_12_pos_next), .clock(clock),
    .pos_next(gpu_str_mem_13_pos_next));
  gpu_str_mem gpu_str_mem_14 (
    .data(data), .addr(addr), .str(str13), .pos(gpu_str_mem_13_pos_next), .clock(clock),
    .pos_next(gpu_str_mem_14_pos_next));
  gpu_str_mem gpu_str_mem_15 (
    .data(data), .addr(addr), .str(str0_2), .pos(gpu_str_mem_17_pos_next), .clock(clock),
    .pos_next(gpu_str_mem_15_pos_next));
  gpu_str_mem gpu_str_mem_16 (
    .data(data), .addr(addr), .str(_14), .pos(gpu_str_mem_14_pos_next), .clock(clock),
    .pos_next(gpu_str_mem_16_pos_next));
  gpu_str_mem gpu_str_mem_17 (
    .data(data), .addr(addr), .str(str15), .pos(gpu_str_mem_16_pos_next), .clock(clock),
    .pos_next(gpu_str_mem_17_pos_next));
  gpu_str_mem gpu_str_mem_18 (
    .data(data), .addr(addr), .str(str1_2), .pos(gpu_str_mem_15_pos_next), .clock(clock),
    .pos_next(gpu_str_mem_18_pos_next));
  gpu_str_mem gpu_str_mem_19 (
    .data(data), .addr(addr), .str(str2_2), .pos(gpu_str_mem_18_pos_next), .clock(clock),
    .pos_next(gpu_str_mem_19_pos_next));
  gpu_str_mem gpu_str_mem_20 (
    .data(data), .addr(addr), .str(str3_2), .pos(gpu_str_mem_19_pos_next), .clock(clock),
    .pos_next(gpu_str_mem_20_pos_next));
  gpu_str_mem gpu_str_mem_21 (
    .data(data), .addr(addr), .str(str4_2), .pos(gpu_str_mem_20_pos_next), .clock(clock),
    .pos_next(gpu_str_mem_21_pos_next));
  gpu_str_mem gpu_str_mem_22 (
    .data(data), .addr(addr), .str(str5_2), .pos(gpu_str_mem_21_pos_next), .clock(clock),
    .pos_next(gpu_str_mem_22_pos_next));
  gpu_str_mem gpu_str_mem_23 (
    .data(data), .addr(addr), .str(str8_2), .pos(gpu_str_mem_24_pos_next), .clock(clock),
    .pos_next(gpu_str_mem_23_pos_next));
  gpu_str_mem gpu_str_mem_24 (
    .data(data), .addr(addr), .str(str7_2), .pos(gpu_str_mem_25_pos_next), .clock(clock),
    .pos_next(gpu_str_mem_24_pos_next));
  gpu_str_mem gpu_str_mem_25 (
    .data(data), .addr(addr), .str(str6_2), .pos(gpu_str_mem_22_pos_next), .clock(clock),
    .pos_next(gpu_str_mem_25_pos_next));
  gpu_str_mem gpu_str_mem_26 (
    .data(data), .addr(addr), .str(str9_2), .pos(gpu_str_mem_23_pos_next), .clock(clock),
    .pos_next(gpu_str_mem_26_pos_next));
  gpu_str_mem gpu_str_mem_27 (
    .data(data), .addr(addr), .str(str10_2), .pos(gpu_str_mem_26_pos_next), .clock(clock),
    .pos_next(gpu_str_mem_27_pos_next));
  gpu_str_mem gpu_str_mem_28 (
    .data(data), .addr(addr), .str(str11_2), .pos(gpu_str_mem_27_pos_next), .clock(clock),
    .pos_next(gpu_str_mem_28_pos_next));
  gpu_str_mem gpu_str_mem_29 (
    .data(data), .addr(addr), .str(str13_2), .pos(gpu_str_mem_30_pos_next), .clock(clock),
    .pos_next(gpu_str_mem_29_pos_next));
  gpu_str_mem gpu_str_mem_30 (
    .data(data), .addr(addr), .str(str12_2), .pos(gpu_str_mem_28_pos_next), .clock(clock),
    .pos_next(gpu_str_mem_30_pos_next));
  gpu_str_mem gpu_str_mem_31 (
    .data(data), .addr(addr), .str(_14_2), .pos(gpu_str_mem_29_pos_next), .clock(clock),
    .pos_next(gpu_str_mem_31_pos_next));
  gpu_str_mem gpu_str_mem_32 (
    .data(data), .addr(addr), .str({corners_out[2], str15_2[14:1], corners_out[3]}),
    .pos(gpu_str_mem_31_pos_next), .clock(clock), .pos_next(next_pos));

  assign addr_pass = addr;
  assign clock_out = clock;
  assign data_pass = data;
  assign {str0[15], str0[0]} = corners_out[1:0];
  assign {str15_2[15], str15_2[0]} = {corners_out[2], corners_out[3]};
  assign str_down_out = {corners_out[2], _14_2[15], str13_2[15], str12_2[15], str11_2[15], str10_2[15], str9_2[15], str8_2[15], str7_2[15], str6_2[15], str5_2[15], str4_2[15], str3_2[15], str2_2[15], str1_2[15], str0_2[15], str15[15], _14[15], str13[15], str12[15], str11[15], str10[15], str9[15], str8[15], str7[15], str6[15], str5[15], str4[15], str3[15], str2[15], str1[15], corners_out[1]};
  assign str_left_out = str1;
  assign str_right_out = {corners_out[2], str15_2[14:1], corners_out[3]};
  assign str_up_out = {corners_out[3], _14_2[0], str13_2[0], str12_2[0], str11_2[0], str10_2[0], str9_2[0], str8_2[0], str7_2[0], str6_2[0], str5_2[0], str4_2[0], str3_2[0], str2_2[0], str1_2[0], str0_2[0], str15[0], _14[0], str13[0], str12[0], str11[0], str10[0], str9[0], str8[0], str7[0], str6[0], str5[0], str4[0], str3[0], str2[0], str1[0], corners_out[0]};

  // Other names for the same wires on the sheet: down0 = corners_out[1]; str14[15:0] = _14; str16[15:0] = str0_2;
  //   str17[15:0] = str1_2; str18[15:0] = str2_2; str19[15:0] = str3_2; str20[15:0] = str4_2; str21[15:0] = str5_2;
  //   str22[15:0] = str6_2; str23[15:0] = str7_2; str24[15:0] = str8_2; str25[15:0] = str9_2; str26[15:0] = str10_2;
  //   str27[15:0] = str11_2; str28[15:0] = str12_2; str29[15:0] = str13_2; str30[15:0] = _14_2; down30 = _14_2[15];
  //   str31[15:0] = {corners_out[2], str15_2[14:1], corners_out[3]}; down31 = corners_out[2]; down1 = str1[15];
  //   down2 = str2[15]; down3 = str3[15]; down4 = str4[15]; down5 = str5[15]; down6 = str6[15]; down7 = str7[15];
  //   down8 = str8[15]; down9 = str9[15]; down10 = str10[15]; down11 = str11[15]; down12 = str12[15];
  //   down13 = str13[15]; down14 = _14[15]; down15 = str15[15]; down16 = str0_2[15]; down17 = str1_2[15];
  //   down18 = str2_2[15]; down19 = str3_2[15]; down20 = str4_2[15]; down21 = str5_2[15]; down22 = str6_2[15];
  //   down23 = str7_2[15]; down24 = str8_2[15]; down25 = str9_2[15]; down26 = str10_2[15]; down27 = str11_2[15];
  //   down28 = str12_2[15]; down29 = str13_2[15]; up0 = corners_out[0]; up1 = str1[0]; up2 = str2[0]; up3 = str3[0];
  //   up4 = str4[0]; up5 = str5[0]; up6 = str6[0]; up7 = str7[0]; up8 = str8[0]; up9 = str9[0]; up10 = str10[0];
  //   up11 = str11[0]; up12 = str12[0]; up13 = str13[0]; up14 = _14[0]; up15 = str15[0]; up16 = str0_2[0];
  //   up17 = str1_2[0]; up18 = str2_2[0]; up19 = str3_2[0]; up20 = str4_2[0]; up21 = str5_2[0]; up22 = str6_2[0];
  //   up23 = str7_2[0]; up24 = str8_2[0]; up25 = str9_2[0]; up26 = str10_2[0]; up27 = str11_2[0]; up28 = str12_2[0];
  //   up29 = str13_2[0]; up30 = _14_2[0]; up31 = corners_out[3]

  // Notes on the sheet:
  //   *ВСТАВЬТЕ ВИДЕОКАРТУ*
endmodule

// CU
module cu (
  input  \cell ,
  input  [7:0] neighbors,
  output new_gen
);

  wire comparator_1_eq, comparator_2_eq, or_1_out;
  wire [3:0] bitadder_1_out;

  BitAdder bitadder_1 (.in0(neighbors), .out(bitadder_1_out));
  Comparator #(.width(4), .mode("unsigned")) comparator_1 (
    .a(bitadder_1_out), .b(4'b0011), .eq(comparator_1_eq));  // open: gt, lt
  Comparator #(.width(4), .mode("unsigned")) comparator_2 (
    .a(bitadder_1_out), .b(4'b0010), .eq(comparator_2_eq));  // open: gt, lt
  or or_1 (or_1_out, comparator_1_eq, comparator_2_eq);
  Multiplexer multiplexer_1 (.in0(comparator_1_eq), .in1(or_1_out), .out(new_gen), .sel(\cell ));  // open: en
endmodule

// COMPUTE\nUNITS
module cu_block (
  input  [15:0] left_row,
  input  [15:0] center_row,
  input  [15:0] right_row,
  input  [5:0] cycle,
  output [15:0] computed_row
);

  cu _15 (
    .\cell (center_row[15]),
    .neighbors({cycle[4:3], right_row[15:14], center_row[14], left_row[14], left_row[15], cycle[5]}),
    .new_gen(computed_row[15]));
  cu _14 (
    .\cell (center_row[14]),
    .neighbors({center_row[15], right_row[15:13], center_row[13], left_row[13], left_row[14], left_row[15]}),
    .new_gen(computed_row[14]));
  cu _13 (
    .\cell (center_row[13]),
    .neighbors({center_row[14], right_row[14:12], center_row[12], left_row[12], left_row[13], left_row[14]}),
    .new_gen(computed_row[13]));
  cu _12 (
    .\cell (center_row[12]),
    .neighbors({center_row[13], right_row[13:11], center_row[11], left_row[11], left_row[12], left_row[13]}),
    .new_gen(computed_row[12]));
  cu _11 (
    .\cell (center_row[11]),
    .neighbors({center_row[12], right_row[12:10], center_row[10], left_row[10], left_row[11], left_row[12]}),
    .new_gen(computed_row[11]));
  cu _10 (
    .\cell (center_row[10]),
    .neighbors({center_row[11], right_row[11:9], center_row[9], left_row[9], left_row[10], left_row[11]}),
    .new_gen(computed_row[10]));
  cu _9 (
    .\cell (center_row[9]),
    .neighbors({center_row[10], right_row[10:8], center_row[8], left_row[8], left_row[9], left_row[10]}),
    .new_gen(computed_row[9]));
  cu _8 (
    .\cell (center_row[8]),
    .neighbors({center_row[9], right_row[9:7], center_row[7], left_row[7], left_row[8], left_row[9]}),
    .new_gen(computed_row[8]));
  cu _7 (
    .\cell (center_row[7]),
    .neighbors({center_row[8], right_row[8:6], center_row[6], left_row[6], left_row[7], left_row[8]}),
    .new_gen(computed_row[7]));
  cu _6 (
    .\cell (center_row[6]),
    .neighbors({center_row[7], right_row[7:5], center_row[5], left_row[5], left_row[6], left_row[7]}),
    .new_gen(computed_row[6]));
  cu _5 (
    .\cell (center_row[5]),
    .neighbors({center_row[6], right_row[6:4], center_row[4], left_row[4], left_row[5], left_row[6]}),
    .new_gen(computed_row[5]));
  cu _4 (
    .\cell (center_row[4]),
    .neighbors({center_row[5], right_row[5:3], center_row[3], left_row[3], left_row[4], left_row[5]}),
    .new_gen(computed_row[4]));
  cu _3 (
    .\cell (center_row[3]),
    .neighbors({center_row[4], right_row[4:2], center_row[2], left_row[2], left_row[3], left_row[4]}),
    .new_gen(computed_row[3]));
  cu _2 (
    .\cell (center_row[2]),
    .neighbors({center_row[3], right_row[3:1], center_row[1], left_row[1], left_row[2], left_row[3]}),
    .new_gen(computed_row[2]));
  cu _1 (
    .\cell (center_row[1]),
    .neighbors({center_row[2], right_row[2:0], center_row[1], left_row[0], left_row[1], left_row[2]}),
    .new_gen(computed_row[1]));
  cu _0 (
    .\cell (center_row[0]),
    .neighbors({center_row[1], right_row[1:0], cycle[0], cycle[1], cycle[2], left_row[0], left_row[1]}),
    .new_gen(computed_row[0]));
endmodule

// GPU\nCOMPUTE MODULE
module gpu_compute_module (
  input  [15:0] str0,
  input  [15:0] str1,
  input  [15:0] str2,
  input  [15:0] str3,
  input  [15:0] str4,
  input  [15:0] str5,
  input  [15:0] str6,
  input  [15:0] str7,
  input  [15:0] str8,
  input  [15:0] str9,
  input  [15:0] str10,
  input  [15:0] str11,
  input  [15:0] str12,
  input  [15:0] str13,
  input  [15:0] str14,
  input  [15:0] str15,
  input  [15:0] str16,
  input  [15:0] str17,
  input  [15:0] str18,
  input  [15:0] str19,
  input  [15:0] str20,
  input  [15:0] str21,
  input  [15:0] str22,
  input  [15:0] str23,
  input  [15:0] str24,
  input  [15:0] str25,
  input  [15:0] str26,
  input  [15:0] str27,
  input  [15:0] str28,
  input  [15:0] str29,
  input  [15:0] str30,
  input  [15:0] str31,
  input  [17:0] str_right,
  input  [17:0] str_left,
  input  [31:0] str_up,
  input  [31:0] str_down,
  output [15:0] next_gen0,
  output [15:0] next_gen1,
  output [15:0] next_gen2,
  output [15:0] next_gen3,
  output [15:0] next_gen4,
  output [15:0] next_gen5,
  output [15:0] next_gen6,
  output [15:0] next_gen7,
  output [15:0] next_gen8,
  output [15:0] next_gen9,
  output [15:0] next_gen10,
  output [15:0] next_gen11,
  output [15:0] next_gen12,
  output [15:0] next_gen13,
  output [15:0] next_gen14,
  output [15:0] next_gen15,
  output [15:0] next_gen15_2,
  output [15:0] next_gen17,
  output [15:0] next_gen18,
  output [15:0] next_gen19,
  output [15:0] next_gen20,
  output [15:0] next_gen21,
  output [15:0] next_gen22,
  output [15:0] next_gen23,
  output [15:0] next_gen24,
  output [15:0] next_gen25,
  output [15:0] next_gen26,
  output [15:0] next_gen27,
  output [15:0] next_gen28,
  output [15:0] next_gen29,
  output [15:0] next_gen30,
  output [15:0] next_gen31
);

  cu_block _0 (
    .left_row(str_left[16:1]), .center_row(str0), .right_row(str1),
    .cycle({str_left[17], str_up[1:0], str_left[0], str_down[1:0]}), .computed_row(next_gen0));
  cu_block _1 (
    .left_row(str0), .center_row(str1), .right_row(str2), .cycle({str_up[2:0], str_down[2:0]}),
    .computed_row(next_gen1));
  cu_block _2 (
    .left_row(str1), .center_row(str2), .right_row(str3), .cycle({str_up[3:1], str_down[3:1]}),
    .computed_row(next_gen2));
  cu_block _3 (
    .left_row(str2), .center_row(str3), .right_row(str4), .cycle({str_up[4:2], str_down[4:2]}),
    .computed_row(next_gen3));
  cu_block _4 (
    .left_row(str3), .center_row(str4), .right_row(str5), .cycle({str_up[5:3], str_down[5:3]}),
    .computed_row(next_gen4));
  cu_block _5 (
    .left_row(str4), .center_row(str5), .right_row(str6), .cycle({str_up[6:4], str_down[6:4]}),
    .computed_row(next_gen5));
  cu_block _6 (
    .left_row(str5), .center_row(str6), .right_row(str7), .cycle({str_up[7:5], str_down[7:5]}),
    .computed_row(next_gen6));
  cu_block _7 (
    .left_row(str6), .center_row(str7), .right_row(str8), .cycle({str_up[8:6], str_down[8:6]}),
    .computed_row(next_gen7));
  cu_block _8 (
    .left_row(str7), .center_row(str8), .right_row(str9), .cycle({str_up[9:7], str_down[9:7]}),
    .computed_row(next_gen8));
  cu_block _9 (
    .left_row(str8), .center_row(str9), .right_row(str10), .cycle({str_up[10:8], str_down[10:8]}),
    .computed_row(next_gen9));
  cu_block _10 (
    .left_row(str9), .center_row(str10), .right_row(str11), .cycle({str_up[11:9], str_down[11:9]}),
    .computed_row(next_gen10));
  cu_block _11 (
    .left_row(str10), .center_row(str11), .right_row(str12), .cycle({str_up[12:10], str_down[12:10]}),
    .computed_row(next_gen11));
  cu_block _12 (
    .left_row(str11), .center_row(str12), .right_row(str13), .cycle({str_up[13:11], str_down[13:11]}),
    .computed_row(next_gen12));
  cu_block _13 (
    .left_row(str12), .center_row(str13), .right_row(str14), .cycle({str_up[14:12], str_down[14:12]}),
    .computed_row(next_gen13));
  cu_block _14 (
    .left_row(str13), .center_row(str14), .right_row(str15), .cycle({str_up[15:13], str_down[15:13]}),
    .computed_row(next_gen14));
  cu_block _15 (
    .left_row(str14), .center_row(str15), .right_row(str16), .cycle({str_up[16:14], str_down[16:14]}),
    .computed_row(next_gen15));
  cu_block _16 (
    .left_row(str15), .center_row(str16), .right_row(str17), .cycle({str_up[17:15], str_down[17:15]}),
    .computed_row(next_gen15_2));
  cu_block _17 (
    .left_row(str16), .center_row(str17), .right_row(str18), .cycle({str_up[18:16], str_down[18:16]}),
    .computed_row(next_gen17));
  cu_block _18 (
    .left_row(str17), .center_row(str18), .right_row(str19), .cycle({str_up[19:17], str_down[19:17]}),
    .computed_row(next_gen18));
  cu_block _19 (
    .left_row(str18), .center_row(str19), .right_row(str20), .cycle({str_up[20:18], str_down[20:18]}),
    .computed_row(next_gen19));
  cu_block _20 (
    .left_row(str19), .center_row(str20), .right_row(str21), .cycle({str_up[21:19], str_down[21:19]}),
    .computed_row(next_gen20));
  cu_block _21 (
    .left_row(str20), .center_row(str21), .right_row(str22), .cycle({str_up[22:20], str_down[22:20]}),
    .computed_row(next_gen21));
  cu_block _22 (
    .left_row(str21), .center_row(str22), .right_row(str23), .cycle({str_up[23:21], str_down[23:21]}),
    .computed_row(next_gen22));
  cu_block _24 (
    .left_row(str23), .center_row(str24), .right_row(str25), .cycle({str_up[25:23], str_down[25:23]}),
    .computed_row(next_gen24));
  cu_block _23 (
    .left_row(str22), .center_row(str23), .right_row(str24), .cycle({str_up[24:22], str_down[24:22]}),
    .computed_row(next_gen23));
  cu_block _25 (
    .left_row(str24), .center_row(str25), .right_row(str26), .cycle({str_up[26:24], str_down[26:24]}),
    .computed_row(next_gen25));
  cu_block _26 (
    .left_row(str25), .center_row(str26), .right_row(str27), .cycle({str_up[27:25], str_down[27:25]}),
    .computed_row(next_gen26));
  cu_block _27 (
    .left_row(str26), .center_row(str27), .right_row(str28), .cycle({str_up[28:26], str_down[28:26]}),
    .computed_row(next_gen27));
  cu_block _28 (
    .left_row(str27), .center_row(str28), .right_row(str29), .cycle({str_up[29:27], str_down[29:27]}),
    .computed_row(next_gen28));
  cu_block _29 (
    .left_row(str28), .center_row(str29), .right_row(str30), .cycle({str_up[30:28], str_down[30:28]}),
    .computed_row(next_gen29));
  cu_block _30 (
    .left_row(str29), .center_row(str30), .right_row(str31), .cycle({str_up[31:29], str_down[31:29]}),
    .computed_row(next_gen30));
  cu_block _31 (
    .left_row(str30), .center_row(str31), .right_row(str_right[16:1]),
    .cycle({str_right[17], str_up[31:30], str_right[0], str_down[31:30]}), .computed_row(next_gen31));
endmodule
